// Logisim project Assignment_1 - Copy.circ as structural Verilog: 1 circuit, main circuit main
module main (
  input  in_1,
  input  in_2,
  input  in_3,
  input  in_4,
  input  Set_Alarm,
  input  Set_Time,
  input  in_7,
  input  in_8,
  input  in_9,
  input  in_10,
  input  in_11
);

  wire and_1_out, and_2_out, and_3_out, and_4_out, and_5_out, and_6_out, and_7_out, and_8_out, and_9_out,
       and_10_out, and_11_out, and_12_out, and_13_out, and_14_out, and_15_out, and_16_out, and_17_out,
       and_18_out, and_19_out, and_20_out, and_21_out, and_22_out, and_23_out, and_24_out, and_25_out,
       and_26_out, and_27_out, and_28_out, and_29_out, and_30_out, and_31_out, and_32_out, and_33_out,
       and_34_out, and_35_out, and_36_out, and_37_out, and_38_out, and_39_out, and_40_out, and_41_out,
       and_42_out, and_43_out, and_44_out, and_45_out, and_46_out, and_47_out, and_48_out, and_49_out,
       and_50_out, and_51_out, and_52_out, and_53_out, button_1_out, button_2_out, clock_1_out, clock_2_out,
       clock_3_out, d_ff_1_q, d_ff_2_q, d_ff_2_qn, d_ff_3_q, d_ff_4_q, j_k_ff_18_q, j_k_ff_22_q, j_k_ff_23_q,
       j_k_ff_24_q, j_k_ff_25_q, j_k_ff_26_q, j_k_ff_30_q, j_k_ff_36_q, not_1_out, not_2_out, not_3_out,
       not_4_out, not_6_out, not_7_out, not_8_out, not_9_out, or_1_out, or_2_out, or_3_out, or_4_out,
       or_5_out, or_6_out, or_7_out, or_11_out, or_12_out, or_13_out, or_14_out, or_15_out, switch_1_p2;
  wire [1:0] j_k_ff_10_q;
  wire [2:0] j_k_ff_16_q, j_k_ff_17_q, j_k_ff_42_q, j_k_ff_43_q, or_8_out;
  wire [3:0] j_k_ff_19_q, j_k_ff_20_q, j_k_ff_21_q, j_k_ff_44_q, j_k_ff_45_q, j_k_ff_46_q;

  and and_1 (and_1_out, not_9_out, j_k_ff_17_q[2]);
  and and_2 (and_2_out, not_9_out, clock_3_out);
  J_K_Flip_Flop #(.trigger("falling")) j_k_ff_1 (
    .J(and_11_out), .K(and_11_out), .clk(or_1_out), .Q(j_k_ff_19_q[3]), .reset(or_3_out));  // open: Qn, preset
  or or_1 (or_1_out, button_1_out, j_k_ff_16_q[2]);
  J_K_Flip_Flop #(.trigger("falling")) j_k_ff_2 (
    .J(and_17_out), .K(and_17_out), .clk(or_2_out), .Q(j_k_ff_20_q[3]), .reset(or_5_out));  // open: Qn, preset
  or or_2 (or_2_out, button_2_out, and_1_out);
  J_K_Flip_Flop j_k_ff_3 (
    .J(and_23_out), .K(and_23_out), .clk(and_3_out), .Q(j_k_ff_21_q[3]), .reset(or_7_out));  // open: Qn, preset
  and and_3 (and_3_out, and_2_out, not_8_out);
  J_K_Flip_Flop #(.trigger("falling")) j_k_ff_4 (
    .J(j_k_ff_10_q[0]), .K(j_k_ff_10_q[0]), .clk(j_k_ff_19_q[3]), .Q(j_k_ff_10_q[1]), .reset(and_25_out));  // open: Qn, preset
  J_K_Flip_Flop #(.trigger("falling")) j_k_ff_5 (
    .J(and_12_out), .K(and_12_out), .clk(j_k_ff_20_q[3]), .Q(j_k_ff_16_q[2]), .reset(or_4_out));  // open: Qn, preset
  J_K_Flip_Flop #(.trigger("falling")) j_k_ff_6 (
    .J(and_18_out), .K(and_18_out), .clk(j_k_ff_21_q[3]), .Q(j_k_ff_17_q[2]), .reset(or_6_out));  // open: Qn, preset
  Clock clock_1 (.out(clock_1_out));
  J_K_Flip_Flop #(.trigger("falling")) j_k_ff_7 (
    .J(and_9_out), .K(and_9_out), .clk(or_1_out), .Q(j_k_ff_19_q[2]), .reset(or_3_out));  // open: Qn, preset
  J_K_Flip_Flop #(.trigger("falling")) j_k_ff_8 (
    .J(and_15_out), .K(and_15_out), .clk(or_2_out), .Q(j_k_ff_20_q[2]), .reset(or_5_out));  // open: Qn, preset
  J_K_Flip_Flop j_k_ff_9 (
    .J(and_21_out), .K(and_21_out), .clk(and_3_out), .Q(j_k_ff_21_q[2]), .reset(or_7_out));  // open: Qn, preset
  J_K_Flip_Flop #(.trigger("falling")) j_k_ff_10 (
    .J(switch_1_p2), .K(switch_1_p2), .clk(j_k_ff_19_q[3]), .Q(j_k_ff_10_q[0]), .reset(and_25_out));  // open: Qn, preset
  J_K_Flip_Flop #(.trigger("falling")) j_k_ff_11 (
    .J(j_k_ff_16_q[0]), .K(j_k_ff_16_q[0]), .clk(j_k_ff_20_q[3]), .Q(j_k_ff_16_q[1]), .reset(or_4_out));  // open: Qn, preset
  J_K_Flip_Flop #(.trigger("falling")) j_k_ff_12 (
    .J(j_k_ff_17_q[0]), .K(j_k_ff_17_q[0]), .clk(j_k_ff_21_q[3]), .Q(j_k_ff_17_q[1]), .reset(or_6_out));  // open: Qn, preset
  and and_4 (and_4_out, clock_1_out, in_3);
  J_K_Flip_Flop #(.trigger("falling")) j_k_ff_13 (
    .J(j_k_ff_19_q[0]), .K(j_k_ff_19_q[0]), .clk(or_1_out), .Q(j_k_ff_19_q[1]), .reset(or_3_out));  // open: Qn, preset
  J_K_Flip_Flop #(.trigger("falling")) j_k_ff_14 (
    .J(j_k_ff_20_q[0]), .K(j_k_ff_20_q[0]), .clk(or_2_out), .Q(j_k_ff_20_q[1]), .reset(or_5_out));  // open: Qn, preset
  J_K_Flip_Flop j_k_ff_15 (
    .J(j_k_ff_21_q[0]), .K(j_k_ff_21_q[0]), .clk(and_3_out), .Q(j_k_ff_21_q[1]), .reset(or_7_out));  // open: Qn, preset
  Clock clock_2 (.out(clock_2_out));
  J_K_Flip_Flop #(.trigger("falling")) j_k_ff_16 (
    .J(switch_1_p2), .K(switch_1_p2), .clk(j_k_ff_20_q[3]), .Q(j_k_ff_16_q[0]), .reset(or_4_out));  // open: Qn, preset
  J_K_Flip_Flop #(.trigger("falling")) j_k_ff_17 (
    .J(switch_1_p2), .K(switch_1_p2), .clk(j_k_ff_21_q[3]), .Q(j_k_ff_17_q[0]), .reset(or_6_out));  // open: Qn, preset
  and and_5 (and_5_out, j_k_ff_22_q, j_k_ff_18_q);
  J_K_Flip_Flop #(.trigger("falling")) j_k_ff_18 (
    .J(and_7_out), .K(and_7_out), .clk(and_4_out), .Q(j_k_ff_18_q), .reset(and_5_out));  // open: Qn, preset
  LED led_1 (.in(j_k_ff_18_q));
  not not_1 (not_1_out, in_3);
  J_K_Flip_Flop #(.trigger("falling")) j_k_ff_19 (
    .J(switch_1_p2), .K(switch_1_p2), .clk(or_1_out), .Q(j_k_ff_19_q[0]), .reset(or_3_out));  // open: Qn, preset
  J_K_Flip_Flop #(.trigger("falling")) j_k_ff_20 (
    .J(switch_1_p2), .K(switch_1_p2), .clk(or_2_out), .Q(j_k_ff_20_q[0]), .reset(or_5_out));  // open: Qn, preset
  J_K_Flip_Flop j_k_ff_21 (
    .J(switch_1_p2), .K(switch_1_p2), .clk(and_3_out), .Q(j_k_ff_21_q[0]), .reset(or_7_out));  // open: Qn, preset
  and and_6 (and_6_out, not_1_out, clock_2_out);
  not not_2 (not_2_out, j_k_ff_19_q[2]);
  not not_3 (not_3_out, j_k_ff_19_q[1]);
  not not_4 (not_4_out, j_k_ff_19_q[3]);
  and and_7 (and_7_out, j_k_ff_23_q, j_k_ff_22_q);
  J_K_Flip_Flop #(.trigger("falling")) j_k_ff_22 (
    .J(j_k_ff_23_q), .K(j_k_ff_23_q), .clk(and_4_out), .Q(j_k_ff_22_q), .reset(and_5_out));  // open: Qn, preset
  LED led_2 (.in(j_k_ff_22_q));
  and and_8 (and_8_out, j_k_ff_19_q[0], j_k_ff_19_q[1]);
  and and_9 (and_9_out, j_k_ff_19_q[1], j_k_ff_19_q[0]);
  or or_3 (or_3_out, and_25_out, and_10_out);
  and and_10 (and_10_out, j_k_ff_19_q[1], j_k_ff_19_q[3]);
  and and_11 (and_11_out, and_8_out, j_k_ff_19_q[2]);
  and and_12 (and_12_out, j_k_ff_16_q[1], j_k_ff_16_q[0]);
  or or_4 (or_4_out, and_25_out, and_13_out);
  and and_13 (and_13_out, j_k_ff_16_q[1], j_k_ff_16_q[2]);
  and and_14 (and_14_out, j_k_ff_20_q[0], j_k_ff_20_q[1]);
  and and_15 (and_15_out, j_k_ff_20_q[1], j_k_ff_20_q[0]);
  or or_5 (or_5_out, and_25_out, and_16_out);
  and and_16 (and_16_out, j_k_ff_20_q[1], j_k_ff_20_q[3]);
  and and_17 (and_17_out, and_14_out, j_k_ff_20_q[2]);
  and and_18 (and_18_out, j_k_ff_17_q[1], j_k_ff_17_q[0]);
  or or_6 (or_6_out, and_25_out, and_19_out);
  and and_19 (and_19_out, j_k_ff_17_q[1], j_k_ff_17_q[2]);
  and and_20 (and_20_out, j_k_ff_21_q[0], j_k_ff_21_q[1]);
  and and_21 (and_21_out, j_k_ff_21_q[1], j_k_ff_21_q[0]);
  or or_7 (or_7_out, and_25_out, and_22_out);
  and and_22 (and_22_out, j_k_ff_21_q[1], j_k_ff_21_q[3]);
  and and_23 (and_23_out, and_20_out, j_k_ff_21_q[2]);
  and and_24 (and_24_out, j_k_ff_19_q[0], j_k_ff_10_q[0], not_2_out, not_3_out, not_4_out);
  and and_25 (and_25_out, j_k_ff_10_q[0], j_k_ff_19_q[1]);
  J_K_Flip_Flop #(.trigger("falling")) j_k_ff_23 (
    .J(in_1), .K(in_1), .clk(and_4_out), .Q(j_k_ff_23_q), .reset(and_5_out));  // open: Qn, preset
  LED led_3 (.in(j_k_ff_23_q));
  and and_26 (and_26_out, and_24_out, and_28_out);
  and and_27 (and_27_out, j_k_ff_25_q, j_k_ff_24_q);
  J_K_Flip_Flop #(.trigger("falling")) j_k_ff_24 (
    .J(and_29_out), .K(and_29_out), .clk(and_6_out), .Q(j_k_ff_24_q), .reset(and_27_out));  // open: Qn, preset
  and and_28 (and_28_out, j_k_ff_16_q[2], j_k_ff_16_q[0]);
  D_Flip_Flop d_ff_1 (.D(j_k_ff_18_q), .clk(and_4_out), .Q(d_ff_1_q));  // open: Qn, preset, reset
  LED led_4 (.in(j_k_ff_24_q));
  // NOT_Gate not_5 has open pins: in=j_k_ff_16_q[1], out=open
  D_Flip_Flop d_ff_2 (.D(d_ff_2_qn), .clk(and_26_out), .Q(d_ff_2_q), .Qn(d_ff_2_qn));  // open: preset, reset
  and and_29 (and_29_out, j_k_ff_26_q, j_k_ff_25_q);
  J_K_Flip_Flop #(.trigger("falling")) j_k_ff_25 (
    .J(j_k_ff_26_q), .K(j_k_ff_26_q), .clk(and_6_out), .Q(j_k_ff_25_q), .reset(and_27_out));  // open: Qn, preset
  not not_6 (not_6_out, in_3);
  D_Flip_Flop d_ff_3 (.D(j_k_ff_22_q), .clk(and_4_out), .Q(d_ff_3_q));  // open: Qn, preset, reset
  LED led_5 (.in(j_k_ff_25_q));
  J_K_Flip_Flop #(.trigger("falling")) j_k_ff_26 (
    .J(in_4), .K(in_4), .clk(and_6_out), .Q(j_k_ff_26_q), .reset(and_27_out));  // open: Qn, preset
  Hex_Digit_Display hex_digit_display_1 (.value({{2{in_7}}, j_k_ff_10_q}));  // open: dp
  LED led_6 (.in(j_k_ff_26_q));
  LED led_7 (.in(switch_1_p2));
  LED led_8 (.in(switch_1_p2));
  Hex_Digit_Display hex_digit_display_2 (.value(j_k_ff_19_q));  // open: dp
  not not_7 (not_7_out, d_ff_2_q);
  D_Flip_Flop d_ff_4 (.D(j_k_ff_23_q), .clk(and_4_out), .Q(d_ff_4_q));  // open: Qn, preset, reset
  Hex_Digit_Display hex_digit_display_3 (.value({in_8, j_k_ff_16_q}));  // open: dp
  Hex_Digit_Display hex_digit_display_4 (.value(j_k_ff_20_q));  // open: dp
  and and_30 (and_30_out, j_k_ff_26_q, not_6_out);
  LED led_9 (.in(switch_1_p2));
  LED led_10 (.in(switch_1_p2));
  and and_31 (and_31_out, in_3, d_ff_4_q);
  and and_32 (and_32_out, j_k_ff_25_q, not_6_out);
  and and_33 (and_33_out, j_k_ff_24_q, not_6_out);
  Hex_Digit_Display hex_digit_display_5 (.value({in_10, j_k_ff_17_q}));  // open: dp
  Hex_Digit_Display hex_digit_display_6 (.value(j_k_ff_21_q));  // open: dp
  and and_34 (and_34_out, in_3, d_ff_3_q);
  and and_35 (and_35_out, in_3, d_ff_1_q);
  not not_8 (not_8_out, Set_Alarm);
  LED led_11 (.in(d_ff_2_q));
  LED led_12 (.in(not_7_out));
  D_Flip_Flop d_ff_5 (.D(j_k_ff_30_q), .clk(j_k_ff_44_q[3]));  // open: Q, Qn, preset, reset
  or or_8 (or_8_out[0], and_31_out, and_30_out);
  or or_9 (or_8_out[1], and_34_out, and_32_out);
  or or_10 (or_8_out[2], and_35_out, and_33_out);
  Hex_Digit_Display hex_digit_display_7 (.value({in_2, or_8_out}));  // open: dp
  not not_9 (not_9_out, Set_Time);
  // Switch switch_1: pin names not known; wires that end beside it: 1'b1, switch_1_p2
  Button button_1 (.out(button_1_out));
  Button button_2 (.out(button_2_out));
  Clock clock_3 (.out(clock_3_out));
  D_Flip_Flop d_ff_6 (.D(j_k_ff_36_q), .clk(j_k_ff_44_q[3]));  // open: Q, Qn, preset, reset
  and and_36 (and_36_out, clock_3_out, Set_Alarm);
  J_K_Flip_Flop #(.trigger("falling")) j_k_ff_27 (
    .J(and_40_out), .K(and_40_out), .clk(j_k_ff_42_q[2]), .Q(j_k_ff_44_q[3]), .reset(or_11_out));  // open: Qn, preset
  J_K_Flip_Flop #(.trigger("falling")) j_k_ff_28 (
    .J(and_46_out), .K(and_46_out), .clk(j_k_ff_43_q[2]), .Q(j_k_ff_45_q[3]), .reset(or_13_out));  // open: Qn, preset
  J_K_Flip_Flop j_k_ff_29 (
    .J(and_52_out), .K(and_52_out), .clk(and_36_out), .Q(j_k_ff_46_q[3]), .reset(or_15_out));  // open: Qn, preset
  J_K_Flip_Flop #(.trigger("falling")) j_k_ff_30 (
    .J(j_k_ff_36_q), .K(j_k_ff_36_q), .clk(j_k_ff_44_q[3]), .Q(j_k_ff_30_q), .reset(and_53_out));  // open: Qn, preset
  J_K_Flip_Flop #(.trigger("falling")) j_k_ff_31 (
    .J(and_41_out), .K(and_41_out), .clk(j_k_ff_45_q[3]), .Q(j_k_ff_42_q[2]), .reset(or_12_out));  // open: Qn, preset
  J_K_Flip_Flop #(.trigger("falling")) j_k_ff_32 (
    .J(and_47_out), .K(and_47_out), .clk(j_k_ff_46_q[3]), .Q(j_k_ff_43_q[2]), .reset(or_14_out));  // open: Qn, preset
  J_K_Flip_Flop #(.trigger("falling")) j_k_ff_33 (
    .J(and_38_out), .K(and_38_out), .clk(j_k_ff_42_q[2]), .Q(j_k_ff_44_q[2]), .reset(or_11_out));  // open: Qn, preset
  J_K_Flip_Flop #(.trigger("falling")) j_k_ff_34 (
    .J(and_44_out), .K(and_44_out), .clk(j_k_ff_43_q[2]), .Q(j_k_ff_45_q[2]), .reset(or_13_out));  // open: Qn, preset
  J_K_Flip_Flop j_k_ff_35 (
    .J(and_50_out), .K(and_50_out), .clk(and_36_out), .Q(j_k_ff_46_q[2]), .reset(or_15_out));  // open: Qn, preset
  J_K_Flip_Flop #(.trigger("falling")) j_k_ff_36 (
    .J(switch_1_p2), .K(switch_1_p2), .clk(j_k_ff_44_q[3]), .Q(j_k_ff_36_q), .reset(and_53_out));  // open: Qn, preset
  J_K_Flip_Flop #(.trigger("falling")) j_k_ff_37 (
    .J(j_k_ff_42_q[0]), .K(j_k_ff_42_q[0]), .clk(j_k_ff_45_q[3]), .Q(j_k_ff_42_q[1]), .reset(or_12_out));  // open: Qn, preset
  J_K_Flip_Flop #(.trigger("falling")) j_k_ff_38 (
    .J(j_k_ff_43_q[0]), .K(j_k_ff_43_q[0]), .clk(j_k_ff_46_q[3]), .Q(j_k_ff_43_q[1]), .reset(or_14_out));  // open: Qn, preset
  J_K_Flip_Flop #(.trigger("falling")) j_k_ff_39 (
    .J(j_k_ff_44_q[0]), .K(j_k_ff_44_q[0]), .clk(j_k_ff_42_q[2]), .Q(j_k_ff_44_q[1]), .reset(or_11_out));  // open: Qn, preset
  J_K_Flip_Flop #(.trigger("falling")) j_k_ff_40 (
    .J(j_k_ff_45_q[0]), .K(j_k_ff_45_q[0]), .clk(j_k_ff_43_q[2]), .Q(j_k_ff_45_q[1]), .reset(or_13_out));  // open: Qn, preset
  J_K_Flip_Flop j_k_ff_41 (
    .J(j_k_ff_46_q[0]), .K(j_k_ff_46_q[0]), .clk(and_36_out), .Q(j_k_ff_46_q[1]), .reset(or_15_out));  // open: Qn, preset
  J_K_Flip_Flop #(.trigger("falling")) j_k_ff_42 (
    .J(switch_1_p2), .K(switch_1_p2), .clk(j_k_ff_45_q[3]), .Q(j_k_ff_42_q[0]), .reset(or_12_out));  // open: Qn, preset
  J_K_Flip_Flop #(.trigger("falling")) j_k_ff_43 (
    .J(switch_1_p2), .K(switch_1_p2), .clk(j_k_ff_46_q[3]), .Q(j_k_ff_43_q[0]), .reset(or_14_out));  // open: Qn, preset
  J_K_Flip_Flop #(.trigger("falling")) j_k_ff_44 (
    .J(switch_1_p2), .K(switch_1_p2), .clk(j_k_ff_42_q[2]), .Q(j_k_ff_44_q[0]), .reset(or_11_out));  // open: Qn, preset
  J_K_Flip_Flop #(.trigger("falling")) j_k_ff_45 (
    .J(switch_1_p2), .K(switch_1_p2), .clk(j_k_ff_43_q[2]), .Q(j_k_ff_45_q[0]), .reset(or_13_out));  // open: Qn, preset
  J_K_Flip_Flop j_k_ff_46 (
    .J(switch_1_p2), .K(switch_1_p2), .clk(and_36_out), .Q(j_k_ff_46_q[0]), .reset(or_15_out));  // open: Qn, preset
  and and_37 (and_37_out, j_k_ff_44_q[0], j_k_ff_44_q[1]);
  and and_38 (and_38_out, j_k_ff_44_q[1], j_k_ff_44_q[0]);
  or or_11 (or_11_out, and_53_out, and_39_out);
  and and_39 (and_39_out, j_k_ff_44_q[1], j_k_ff_44_q[3]);
  and and_40 (and_40_out, and_37_out, j_k_ff_44_q[2]);
  and and_41 (and_41_out, j_k_ff_42_q[1], j_k_ff_42_q[0]);
  or or_12 (or_12_out, and_53_out, and_42_out);
  and and_42 (and_42_out, j_k_ff_42_q[1], j_k_ff_42_q[2]);
  and and_43 (and_43_out, j_k_ff_45_q[0], j_k_ff_45_q[1]);
  and and_44 (and_44_out, j_k_ff_45_q[1], j_k_ff_45_q[0]);
  or or_13 (or_13_out, and_53_out, and_45_out);
  and and_45 (and_45_out, j_k_ff_45_q[1], j_k_ff_45_q[3]);
  and and_46 (and_46_out, and_43_out, j_k_ff_45_q[2]);
  and and_47 (and_47_out, j_k_ff_43_q[1], j_k_ff_43_q[0]);
  or or_14 (or_14_out, and_53_out, and_48_out);
  and and_48 (and_48_out, j_k_ff_43_q[1], j_k_ff_43_q[2]);
  and and_49 (and_49_out, j_k_ff_46_q[0], j_k_ff_46_q[1]);
  and and_50 (and_50_out, j_k_ff_46_q[1], j_k_ff_46_q[0]);
  or or_15 (or_15_out, and_53_out, and_51_out);
  and and_51 (and_51_out, j_k_ff_46_q[1], j_k_ff_46_q[3]);
  and and_52 (and_52_out, and_49_out, j_k_ff_46_q[2]);
  and and_53 (and_53_out, j_k_ff_36_q, j_k_ff_44_q[1]);

  // Notes on the sheet:
  //   AM
  //   PM
  //   On/Off
  //   +hr
  //   +min
endmodule
