// Logisim project Assignment_1.circ as structural Verilog: 1 circuit, main circuit main
module main (
  input  SET_ALARM,
  input  SET_TIME,
  input  in_3
);

  wire and_1_out, and_2_out, and_3_out, and_4_out, and_5_out, and_6_out, and_7_out, and_8_out, and_9_out,
       and_10_out, and_11_out, and_12_out, and_13_out, and_14_out, and_15_out, and_16_out, and_17_out,
       and_18_out, and_19_out, and_20_out, and_21_out, and_22_out, and_23_out, and_24_out, and_25_out,
       and_26_out, and_27_out, and_28_out, and_29_out, and_30_out, and_31_out, and_32_out, and_33_out,
       and_34_out, and_35_out, and_36_out, and_37_out, and_38_out, and_39_out, and_40_out, and_41_out,
       and_42_out, and_43_out, and_44_out, and_45_out, and_46_out, and_47_out, and_48_out, and_49_out,
       and_50_out, and_51_out, and_52_out, and_53_out, and_54_out, and_55_out, and_56_out, and_57_out,
       and_58_out, and_59_out, and_60_out, and_61_out, and_62_out, button_1_out, button_2_out, button_3_out,
       clock_1_out, d_ff_1_q, d_ff_1_qn, d_ff_2_q, d_ff_3_q, d_ff_4_q, d_ff_5_q, d_ff_6_q, d_ff_7_q,
       d_ff_8_q, d_ff_9_q, d_ff_10_q, d_ff_11_q, d_ff_12_q, d_ff_13_q, d_ff_14_q, j_k_ff_1_q, j_k_ff_2_q,
       j_k_ff_4_q, j_k_ff_5_q, j_k_ff_7_q, j_k_ff_8_q, j_k_ff_10_q, j_k_ff_11_q, j_k_ff_13_q, j_k_ff_14_q,
       j_k_ff_16_q, j_k_ff_18_q, j_k_ff_19_q, j_k_ff_21_q, j_k_ff_22_q, j_k_ff_23_q, j_k_ff_24_q,
       j_k_ff_25_q, j_k_ff_26_q, j_k_ff_27_q, j_k_ff_28_q, j_k_ff_29_q, j_k_ff_30_q, j_k_ff_31_q,
       j_k_ff_32_q, j_k_ff_33_q, not_1_out, not_2_out, not_3_out, not_4_out, not_5_out, not_7_out, not_8_out,
       not_9_out, or_1_out, or_2_out, or_3_out, or_4_out, or_5_out, or_6_out, or_7_out, or_8_out, or_22_out,
       or_23_out, or_24_out, or_25_out, switch_1_p2, xnor_1_out, xnor_2_out, xnor_3_out, xnor_4_out,
       xnor_5_out, xnor_6_out, xnor_7_out, xnor_8_out, xnor_9_out, xnor_10_out, xnor_11_out, xnor_12_out,
       xnor_13_out;
  wire [1:0] or_9_out;
  wire [2:0] j_k_ff_17_q, or_13_out;
  wire [3:0] j_k_ff_20_q, or_10_out, or_11_out;

  not not_1 (not_1_out, not_9_out);
  not not_2 (not_2_out, not_9_out);
  and and_1 (and_1_out, not_2_out, button_3_out);
  and and_2 (and_2_out, not_9_out, j_k_ff_17_q[2]);
  and and_3 (and_3_out, not_9_out, clock_1_out);
  and and_4 (and_4_out, not_1_out, button_2_out);
  or or_1 (or_1_out, and_1_out, and_2_out);
  J_K_Flip_Flop #(.trigger("falling")) j_k_ff_1 (
    .J(and_11_out), .K(and_11_out), .clk(or_2_out), .Q(j_k_ff_1_q), .reset(or_3_out));  // open: Qn, preset
  or or_2 (or_2_out, and_4_out, j_k_ff_5_q);
  J_K_Flip_Flop #(.trigger("falling")) j_k_ff_2 (
    .J(and_17_out), .K(and_17_out), .clk(or_1_out), .Q(j_k_ff_2_q), .reset(or_5_out));  // open: Qn, preset
  J_K_Flip_Flop j_k_ff_3 (
    .J(and_23_out), .K(and_23_out), .clk(and_3_out), .Q(j_k_ff_20_q[3]), .reset(or_7_out));  // open: Qn, preset
  J_K_Flip_Flop #(.trigger("falling")) j_k_ff_4 (
    .J(j_k_ff_10_q), .K(j_k_ff_10_q), .clk(j_k_ff_1_q), .Q(j_k_ff_4_q), .reset(and_24_out));  // open: Qn, preset
  J_K_Flip_Flop #(.trigger("falling")) j_k_ff_5 (
    .J(and_12_out), .K(and_12_out), .clk(j_k_ff_2_q), .Q(j_k_ff_5_q), .reset(or_4_out));  // open: Qn, preset
  J_K_Flip_Flop #(.trigger("falling")) j_k_ff_6 (
    .J(and_18_out), .K(and_18_out), .clk(j_k_ff_20_q[3]), .Q(j_k_ff_17_q[2]), .reset(or_6_out));  // open: Qn, preset
  J_K_Flip_Flop #(.trigger("falling")) j_k_ff_7 (
    .J(and_9_out), .K(and_9_out), .clk(or_2_out), .Q(j_k_ff_7_q), .reset(or_3_out));  // open: Qn, preset
  J_K_Flip_Flop #(.trigger("falling")) j_k_ff_8 (
    .J(and_15_out), .K(and_15_out), .clk(or_1_out), .Q(j_k_ff_8_q), .reset(or_5_out));  // open: Qn, preset
  J_K_Flip_Flop j_k_ff_9 (
    .J(and_21_out), .K(and_21_out), .clk(and_3_out), .Q(j_k_ff_20_q[2]), .reset(or_7_out));  // open: Qn, preset
  not not_3 (not_3_out, j_k_ff_7_q);
  not not_4 (not_4_out, j_k_ff_13_q);
  not not_5 (not_5_out, j_k_ff_1_q);
  J_K_Flip_Flop #(.trigger("falling")) j_k_ff_10 (
    .J(switch_1_p2), .K(switch_1_p2), .clk(j_k_ff_1_q), .Q(j_k_ff_10_q), .reset(and_24_out));  // open: Qn, preset
  J_K_Flip_Flop #(.trigger("falling")) j_k_ff_11 (
    .J(j_k_ff_16_q), .K(j_k_ff_16_q), .clk(j_k_ff_2_q), .Q(j_k_ff_11_q), .reset(or_4_out));  // open: Qn, preset
  J_K_Flip_Flop #(.trigger("falling")) j_k_ff_12 (
    .J(j_k_ff_17_q[0]), .K(j_k_ff_17_q[0]), .clk(j_k_ff_20_q[3]), .Q(j_k_ff_17_q[1]), .reset(or_6_out));  // open: Qn, preset
  and and_5 (and_5_out, j_k_ff_18_q, j_k_ff_10_q, not_3_out, not_4_out, not_5_out);
  J_K_Flip_Flop #(.trigger("falling")) j_k_ff_13 (
    .J(j_k_ff_18_q), .K(j_k_ff_18_q), .clk(or_2_out), .Q(j_k_ff_13_q), .reset(or_3_out));  // open: Qn, preset
  J_K_Flip_Flop #(.trigger("falling")) j_k_ff_14 (
    .J(j_k_ff_19_q), .K(j_k_ff_19_q), .clk(or_1_out), .Q(j_k_ff_14_q), .reset(or_5_out));  // open: Qn, preset
  J_K_Flip_Flop j_k_ff_15 (
    .J(j_k_ff_20_q[0]), .K(j_k_ff_20_q[0]), .clk(and_3_out), .Q(j_k_ff_20_q[1]), .reset(or_7_out));  // open: Qn, preset
  J_K_Flip_Flop #(.trigger("falling")) j_k_ff_16 (
    .J(switch_1_p2), .K(switch_1_p2), .clk(j_k_ff_2_q), .Q(j_k_ff_16_q), .reset(or_4_out));  // open: Qn, preset
  J_K_Flip_Flop #(.trigger("falling")) j_k_ff_17 (
    .J(switch_1_p2), .K(switch_1_p2), .clk(j_k_ff_20_q[3]), .Q(j_k_ff_17_q[0]), .reset(or_6_out));  // open: Qn, preset
  and and_6 (and_6_out, and_5_out, and_7_out);
  J_K_Flip_Flop #(.trigger("falling")) j_k_ff_18 (
    .J(switch_1_p2), .K(switch_1_p2), .clk(or_2_out), .Q(j_k_ff_18_q), .reset(or_3_out));  // open: Qn, preset
  J_K_Flip_Flop #(.trigger("falling")) j_k_ff_19 (
    .J(switch_1_p2), .K(switch_1_p2), .clk(or_1_out), .Q(j_k_ff_19_q), .reset(or_5_out));  // open: Qn, preset
  J_K_Flip_Flop j_k_ff_20 (
    .J(switch_1_p2), .K(switch_1_p2), .clk(and_3_out), .Q(j_k_ff_20_q[0]), .reset(or_7_out));  // open: Qn, preset
  and and_7 (and_7_out, j_k_ff_5_q, j_k_ff_16_q);
  // NOT_Gate not_6 has open pins: in=j_k_ff_11_q, out=open
  D_Flip_Flop d_ff_1 (.D(d_ff_1_qn), .clk(and_6_out), .Q(d_ff_1_q), .Qn(d_ff_1_qn));  // open: preset, reset
  and and_8 (and_8_out, j_k_ff_18_q, j_k_ff_13_q);
  and and_9 (and_9_out, j_k_ff_13_q, j_k_ff_18_q);
  or or_3 (or_3_out, and_24_out, and_10_out);
  and and_10 (and_10_out, j_k_ff_13_q, j_k_ff_1_q);
  and and_11 (and_11_out, and_8_out, j_k_ff_7_q);
  and and_12 (and_12_out, j_k_ff_11_q, j_k_ff_16_q);
  or or_4 (or_4_out, and_24_out, and_13_out);
  and and_13 (and_13_out, j_k_ff_11_q, j_k_ff_5_q);
  and and_14 (and_14_out, j_k_ff_19_q, j_k_ff_14_q);
  and and_15 (and_15_out, j_k_ff_14_q, j_k_ff_19_q);
  or or_5 (or_5_out, and_24_out, and_16_out);
  and and_16 (and_16_out, j_k_ff_14_q, j_k_ff_2_q);
  and and_17 (and_17_out, and_14_out, j_k_ff_8_q);
  and and_18 (and_18_out, j_k_ff_17_q[1], j_k_ff_17_q[0]);
  or or_6 (or_6_out, and_24_out, and_19_out);
  and and_19 (and_19_out, j_k_ff_17_q[1], j_k_ff_17_q[2]);
  and and_20 (and_20_out, j_k_ff_20_q[0], j_k_ff_20_q[1]);
  and and_21 (and_21_out, j_k_ff_20_q[1], j_k_ff_20_q[0]);
  or or_7 (or_7_out, and_24_out, and_22_out);
  and and_22 (and_22_out, j_k_ff_20_q[1], j_k_ff_20_q[3]);
  and and_23 (and_23_out, and_20_out, j_k_ff_20_q[2]);
  and and_24 (and_24_out, j_k_ff_10_q, j_k_ff_13_q);
  xnor xnor_1 (xnor_1_out, j_k_ff_2_q, d_ff_3_q);
  or or_8 (or_8_out, d_ff_3_q, d_ff_7_q, d_ff_10_q, d_ff_14_q, d_ff_6_q, d_ff_9_q, d_ff_13_q, d_ff_2_q, d_ff_5_q, d_ff_8_q, d_ff_12_q, d_ff_4_q, d_ff_11_q);
  xnor xnor_2 (xnor_2_out, j_k_ff_8_q, d_ff_7_q);
  Hex_Digit_Display hex_digit_display_1 (.value({2'b00, or_9_out}));  // open: dp
  Hex_Digit_Display hex_digit_display_2 (.value(or_10_out));  // open: dp
  or or_9 (or_9_out[0], and_25_out, and_26_out);
  and and_25 (and_25_out, not_8_out, j_k_ff_10_q);
  and and_26 (and_26_out, d_ff_11_q, SET_ALARM);
  or or_10 (or_10_out[0], and_27_out, and_28_out);
  and and_27 (and_27_out, j_k_ff_18_q, not_8_out);
  and and_28 (and_28_out, d_ff_12_q, SET_ALARM);
  and and_29 (and_29_out, j_k_ff_16_q, not_8_out);
  or or_11 (or_11_out[0], and_30_out, and_31_out);
  and and_30 (and_30_out, j_k_ff_19_q, not_8_out);
  and and_31 (and_31_out, d_ff_14_q, SET_ALARM);
  xnor xnor_3 (xnor_3_out, j_k_ff_14_q, d_ff_10_q);
  LED led_1 (.in(switch_1_p2));
  LED led_2 (.in(switch_1_p2));
  not not_7 (not_7_out, d_ff_1_q);
  and and_32 (and_32_out, j_k_ff_4_q, not_8_out);
  or or_12 (or_10_out[1], and_33_out, and_37_out);
  and and_33 (and_33_out, j_k_ff_13_q, not_8_out);
  or or_13 (or_13_out[0], and_29_out, and_34_out);
  and and_34 (and_34_out, d_ff_13_q, SET_ALARM);
  or or_14 (or_11_out[1], and_35_out, and_40_out);
  and and_35 (and_35_out, j_k_ff_14_q, not_8_out);
  xnor xnor_4 (xnor_4_out, j_k_ff_19_q, d_ff_14_q);
  xnor xnor_5 (xnor_5_out, j_k_ff_5_q, d_ff_6_q);
  Hex_Digit_Display hex_digit_display_3 (.value({1'b0, or_13_out}));  // open: dp
  Hex_Digit_Display hex_digit_display_4 (.value(or_11_out));  // open: dp
  or or_15 (or_9_out[1], and_32_out, and_36_out);
  and and_36 (and_36_out, d_ff_4_q, SET_ALARM);
  and and_37 (and_37_out, d_ff_8_q, SET_ALARM);
  or or_16 (or_13_out[1], and_38_out, and_39_out);
  and and_38 (and_38_out, j_k_ff_11_q, not_8_out);
  and and_39 (and_39_out, d_ff_9_q, SET_ALARM);
  and and_40 (and_40_out, d_ff_10_q, SET_ALARM);
  xnor xnor_6 (xnor_6_out, j_k_ff_11_q, d_ff_9_q);
  and and_41 (and_41_out, xnor_1_out, xnor_2_out, xnor_3_out, xnor_4_out, xnor_5_out, xnor_6_out, xnor_7_out, xnor_8_out, xnor_9_out, xnor_10_out, xnor_11_out, xnor_12_out, xnor_13_out);
  LED led_3 (.in(switch_1_p2));
  LED led_4 (.in(switch_1_p2));
  or or_17 (or_10_out[2], and_42_out, and_43_out);
  and and_42 (and_42_out, j_k_ff_7_q, not_8_out);
  and and_43 (and_43_out, d_ff_5_q, SET_ALARM);
  and and_44 (and_44_out, j_k_ff_5_q, not_8_out);
  or or_18 (or_11_out[2], and_45_out, and_46_out);
  and and_45 (and_45_out, j_k_ff_8_q, not_8_out);
  and and_46 (and_46_out, d_ff_7_q, SET_ALARM);
  xnor xnor_7 (xnor_7_out, j_k_ff_16_q, d_ff_13_q);
  not not_8 (not_8_out, SET_ALARM);
  LED led_5 (.in(and_41_out));
  LED led_6 (.in(or_8_out));
  Hex_Digit_Display hex_digit_display_5 (.value({in_3, j_k_ff_17_q}));  // open: dp
  Hex_Digit_Display hex_digit_display_6 (.value(j_k_ff_20_q));  // open: dp
  or or_19 (or_10_out[3], and_47_out, and_50_out);
  and and_47 (and_47_out, j_k_ff_1_q, not_8_out);
  D_Flip_Flop #(.trigger("falling")) d_ff_2 (
    .D(j_k_ff_22_q), .clk(button_2_out), .Q(d_ff_2_q), .reset(button_1_out));  // open: Qn, preset
  or or_20 (or_13_out[2], and_44_out, and_48_out);
  and and_48 (and_48_out, d_ff_6_q, SET_ALARM);
  or or_21 (or_11_out[3], and_49_out, and_51_out);
  and and_49 (and_49_out, j_k_ff_2_q, not_8_out);
  D_Flip_Flop #(.trigger("falling")) d_ff_3 (
    .D(j_k_ff_21_q), .clk(button_3_out), .Q(d_ff_3_q), .reset(button_1_out));  // open: Qn, preset
  xnor xnor_8 (xnor_8_out, j_k_ff_1_q, d_ff_2_q);
  xnor xnor_9 (xnor_9_out, j_k_ff_7_q, d_ff_5_q);
  LED led_7 (.in(d_ff_1_q));
  LED led_8 (.in(not_7_out));
  D_Flip_Flop d_ff_4 (.D(j_k_ff_24_q), .clk(j_k_ff_28_q), .Q(d_ff_4_q), .reset(or_24_out));  // open: Qn, preset
  and and_50 (and_50_out, d_ff_2_q, SET_ALARM);
  and and_51 (and_51_out, d_ff_3_q, SET_ALARM);
  xnor xnor_10 (xnor_10_out, j_k_ff_13_q, d_ff_8_q);
  D_Flip_Flop #(.trigger("falling")) d_ff_5 (
    .D(j_k_ff_26_q), .clk(button_2_out), .Q(d_ff_5_q), .reset(button_1_out));  // open: Qn, preset
  D_Flip_Flop #(.trigger("falling")) d_ff_6 (
    .D(j_k_ff_23_q), .clk(j_k_ff_21_q), .Q(d_ff_6_q), .reset(button_1_out));  // open: Qn, preset
  D_Flip_Flop #(.trigger("falling")) d_ff_7 (
    .D(j_k_ff_25_q), .clk(button_3_out), .Q(d_ff_7_q), .reset(button_1_out));  // open: Qn, preset
  xnor xnor_11 (xnor_11_out, j_k_ff_18_q, d_ff_12_q);
  D_Flip_Flop #(.trigger("falling")) d_ff_8 (
    .D(j_k_ff_30_q), .clk(button_2_out), .Q(d_ff_8_q), .reset(button_1_out));  // open: Qn, preset
  D_Flip_Flop #(.trigger("falling")) d_ff_9 (
    .D(j_k_ff_27_q), .clk(j_k_ff_21_q), .Q(d_ff_9_q), .reset(button_1_out));  // open: Qn, preset
  D_Flip_Flop #(.trigger("falling")) d_ff_10 (
    .D(j_k_ff_29_q), .clk(button_3_out), .Q(d_ff_10_q), .reset(button_1_out));  // open: Qn, preset
  xnor xnor_12 (xnor_12_out, j_k_ff_4_q, d_ff_4_q);
  not not_9 (not_9_out, SET_TIME);
  // Switch switch_1: pin names not known; wires that end beside it: 1'b1, switch_1_p2
  Button button_1 (.out(button_1_out));
  Button button_2 (.out(button_2_out));
  Button button_3 (.out(button_3_out));
  Clock clock_1 (.out(clock_1_out));
  D_Flip_Flop d_ff_11 (.D(j_k_ff_28_q), .clk(j_k_ff_28_q), .Q(d_ff_11_q), .reset(or_24_out));  // open: Qn, preset
  D_Flip_Flop #(.trigger("falling")) d_ff_12 (
    .D(j_k_ff_33_q), .clk(button_2_out), .Q(d_ff_12_q), .reset(button_1_out));  // open: Qn, preset
  D_Flip_Flop #(.trigger("falling")) d_ff_13 (
    .D(j_k_ff_31_q), .clk(j_k_ff_21_q), .Q(d_ff_13_q), .reset(button_1_out));  // open: Qn, preset
  D_Flip_Flop #(.trigger("falling")) d_ff_14 (
    .D(j_k_ff_32_q), .clk(button_3_out), .Q(d_ff_14_q), .reset(button_1_out));  // open: Qn, preset
  xnor xnor_13 (xnor_13_out, j_k_ff_10_q, d_ff_11_q);
  J_K_Flip_Flop j_k_ff_21 (
    .J(and_57_out), .K(and_57_out), .clk(button_3_out), .Q(j_k_ff_21_q), .reset(or_23_out));  // open: Qn, preset
  J_K_Flip_Flop j_k_ff_22 (
    .J(and_61_out), .K(and_61_out), .clk(button_2_out), .Q(j_k_ff_22_q), .reset(or_25_out));  // open: Qn, preset
  J_K_Flip_Flop j_k_ff_23 (
    .J(and_52_out), .K(and_52_out), .clk(j_k_ff_21_q), .Q(j_k_ff_23_q), .reset(or_22_out));  // open: Qn, preset
  J_K_Flip_Flop #(.trigger("falling")) j_k_ff_24 (
    .J(j_k_ff_28_q), .K(j_k_ff_28_q), .clk(j_k_ff_22_q), .Q(j_k_ff_24_q), .reset(or_24_out));  // open: Qn, preset
  J_K_Flip_Flop j_k_ff_25 (
    .J(and_55_out), .K(and_55_out), .clk(button_3_out), .Q(j_k_ff_25_q), .reset(or_23_out));  // open: Qn, preset
  J_K_Flip_Flop j_k_ff_26 (
    .J(and_59_out), .K(and_59_out), .clk(button_2_out), .Q(j_k_ff_26_q), .reset(or_25_out));  // open: Qn, preset
  J_K_Flip_Flop j_k_ff_27 (
    .J(j_k_ff_31_q), .K(j_k_ff_31_q), .clk(j_k_ff_21_q), .Q(j_k_ff_27_q), .reset(or_22_out));  // open: Qn, preset
  J_K_Flip_Flop #(.trigger("falling")) j_k_ff_28 (
    .J(switch_1_p2), .K(switch_1_p2), .clk(j_k_ff_22_q), .Q(j_k_ff_28_q), .reset(or_24_out));  // open: Qn, preset
  J_K_Flip_Flop j_k_ff_29 (
    .J(j_k_ff_32_q), .K(j_k_ff_32_q), .clk(button_3_out), .Q(j_k_ff_29_q), .reset(or_23_out));  // open: Qn, preset
  J_K_Flip_Flop j_k_ff_30 (
    .J(j_k_ff_33_q), .K(j_k_ff_33_q), .clk(button_2_out), .Q(j_k_ff_30_q), .reset(or_25_out));  // open: Qn, preset
  J_K_Flip_Flop j_k_ff_31 (
    .J(switch_1_p2), .K(switch_1_p2), .clk(j_k_ff_21_q), .Q(j_k_ff_31_q), .reset(or_22_out));  // open: Qn, preset
  J_K_Flip_Flop j_k_ff_32 (
    .J(switch_1_p2), .K(switch_1_p2), .clk(button_3_out), .Q(j_k_ff_32_q), .reset(or_23_out));  // open: Qn, preset
  J_K_Flip_Flop j_k_ff_33 (
    .J(switch_1_p2), .K(switch_1_p2), .clk(button_2_out), .Q(j_k_ff_33_q), .reset(or_25_out));  // open: Qn, preset
  or or_22 (or_22_out, and_53_out, button_1_out);
  and and_52 (and_52_out, j_k_ff_27_q, j_k_ff_31_q);
  and and_53 (and_53_out, j_k_ff_27_q, j_k_ff_23_q);
  and and_54 (and_54_out, j_k_ff_32_q, j_k_ff_29_q);
  and and_55 (and_55_out, j_k_ff_29_q, j_k_ff_32_q);
  or or_23 (or_23_out, button_1_out, and_56_out);
  and and_56 (and_56_out, j_k_ff_29_q, j_k_ff_21_q);
  and and_57 (and_57_out, and_54_out, j_k_ff_25_q);
  or or_24 (or_24_out, button_1_out, and_62_out);
  and and_58 (and_58_out, j_k_ff_33_q, j_k_ff_30_q);
  and and_59 (and_59_out, j_k_ff_30_q, j_k_ff_33_q);
  or or_25 (or_25_out, and_62_out, button_1_out, and_60_out);
  and and_60 (and_60_out, j_k_ff_30_q, j_k_ff_22_q);
  and and_61 (and_61_out, and_58_out, j_k_ff_26_q);
  and and_62 (and_62_out, j_k_ff_28_q, j_k_ff_30_q);

  // Notes on the sheet:
  //   Alarm
  //   Alarm ON/OFF
  //   AM
  //   PM
  //   ON/OFF
  //   RESET ALARM
  //   +hr
  //   +min
endmodule
