// Logisim project Lab02.circ as structural Verilog: 1 circuit, main circuit main
module main (
  input  Input_A1,
  input  Input_B1,
  input  Input_B2,
  input  Input_A3,
  input  Input_B4,
  input  DATA,
  input  J,
  input  K
);

  wire and_1_out, and_2_out, and_3_out, and_4_out, and_5_out, and_6_out, and_7_out, and_8_out, and_9_out,
       clock_1_out, clock_2_out, nand_1_out, nand_2_out, nand_3_out, nand_4_out, nor_1_out, nor_2_out,
       nor_3_out, nor_4_out, not_1_out, or_1_out, or_2_out, or_3_out, xor_1_out, xor_2_out, xor_3_out,
       xor_4_out, xor_5_out, xor_6_out, xor_7_out;

  Clock clock_1 (.out(clock_1_out));
  Clock clock_2 (.out(clock_2_out));
  not not_1 (not_1_out, DATA);
  nand nand_1 (nand_1_out, nand_4_out, J, clock_2_out);
  nand nand_2 (nand_2_out, clock_2_out, K, nand_3_out);
  xor xor_1 (xor_1_out, Input_A1, Input_B1);
  and and_1 (and_1_out, Input_A1, Input_B1);
  xor xor_2 (xor_2_out, 1'b1, Input_B2);
  and and_2 (and_2_out, 1'b1, Input_B2);
  xor xor_3 (xor_3_out, Input_A3, 1'b1);
  and and_3 (and_3_out, Input_A3, 1'b1);
  xor xor_4 (xor_4_out, 1'b1, Input_B4);
  and and_4 (and_4_out, 1'b1, Input_B4);
  nor nor_1 (nor_1_out, 1'b1, nor_2_out);
  nor nor_2 (nor_2_out, nor_1_out, 1'b1);
  and and_5 (and_5_out, not_1_out, clock_1_out);
  and and_6 (and_6_out, clock_1_out, DATA);
  nand nand_3 (nand_3_out, nand_1_out, nand_4_out);
  nand nand_4 (nand_4_out, nand_3_out, nand_2_out);
  xor xor_5 (xor_5_out, and_1_out, xor_2_out);
  LED led_1 (.in(nor_1_out));
  LED led_2 (.in(nor_2_out));
  nor nor_3 (nor_3_out, and_5_out, nor_4_out);
  nor nor_4 (nor_4_out, nor_3_out, and_6_out);
  and and_7 (and_7_out, and_1_out, xor_2_out);
  xor xor_6 (xor_6_out, or_1_out, xor_3_out);
  and and_8 (and_8_out, or_1_out, xor_3_out);
  xor xor_7 (xor_7_out, or_2_out, xor_4_out);
  and and_9 (and_9_out, or_2_out, xor_4_out);
  LED led_3 (.in(nor_3_out));
  LED led_4 (.in(nor_4_out));
  LED led_5 (.in(nand_3_out));
  LED led_6 (.in(nand_4_out));
  LED led_7 (.in(xor_1_out));
  LED led_8 (.in(xor_5_out));
  or or_1 (or_1_out, and_7_out, and_2_out);
  LED led_9 (.in(xor_6_out));
  or or_2 (or_2_out, and_8_out, and_3_out);
  LED led_10 (.in(xor_7_out));
  or or_3 (or_3_out, and_9_out, and_4_out);
  LED led_11 (.in(and_1_out));
  LED led_12 (.in(or_1_out));
  LED led_13 (.in(or_2_out));
  LED led_14 (.in(or_3_out));

  // Notes on the sheet:
  //   CLOCK
  //   CLK
  //   Input A2
  //   Input B3
  //   Input A4
  //   SET
  //   RESET
  //   Q
  //   Q'
  //   Q
  //   Q
  //   Q'
  //   Q'
  //   Sum 1
  //   Carry Out 1
  //   Sum 2
  //   Carry Out 2
  //   Sum 3
  //   Sum 4
  //   Carry Out 4
  //   Carry Out 3
endmodule
