// Logisim project Lab_03.circ as structural Verilog: 1 circuit, main circuit main
module main (
  input  in_1,
  input  in_2,
  input  in_3,
  input  in_4,
  input  in_5,
  input  in_6,
  input  in_7
);

  wire and_1_out, and_2_out, and_3_out, and_4_out, clock_1_out, clock_2_out, clock_3_out, clock_4_out,
       j_k_ff_3_q, j_k_ff_4_q, j_k_ff_7_q, j_k_ff_8_q, j_k_ff_11_q, j_k_ff_12_q;
  wire [2:0] j_k_ff_1_q, j_k_ff_10_q;

  Clock clock_1 (.out(clock_1_out));
  Clock clock_2 (.out(clock_2_out));
  Clock clock_3 (.out(clock_3_out));
  Clock clock_4 (.out(clock_4_out));
  J_K_Flip_Flop j_k_ff_1 (
    .J(in_1), .clk(clock_4_out), .K(in_1), .Q(j_k_ff_1_q[0]), .reset(and_4_out));  // open: Qn, preset
  J_K_Flip_Flop j_k_ff_2 (
    .J(in_3), .K(in_3), .clk(j_k_ff_10_q[1]), .Q(j_k_ff_10_q[2]), .reset(in_4));  // open: Qn, preset
  J_K_Flip_Flop j_k_ff_3 (.J(in_6), .clk(clock_2_out), .K(in_6), .Q(j_k_ff_3_q));  // open: Qn, preset, reset
  LED led_1 (.in(j_k_ff_3_q));
  J_K_Flip_Flop j_k_ff_4 (
    .J(in_7), .clk(clock_3_out), .K(in_7), .Q(j_k_ff_4_q), .reset(and_3_out));  // open: Qn, preset
  LED led_2 (.in(j_k_ff_4_q));
  LED led_3 (.in(j_k_ff_1_q[0]));
  LED led_4 (.in(j_k_ff_10_q[2]));
  J_K_Flip_Flop j_k_ff_5 (
    .J(j_k_ff_1_q[0]), .clk(clock_4_out), .K(j_k_ff_1_q[0]), .Q(j_k_ff_1_q[1]), .reset(and_4_out));  // open: Qn, preset
  J_K_Flip_Flop j_k_ff_6 (
    .J(in_3), .K(in_3), .clk(j_k_ff_10_q[0]), .Q(j_k_ff_10_q[1]), .reset(in_4));  // open: Qn, preset
  LED led_5 (.in(j_k_ff_10_q[1]));
  J_K_Flip_Flop j_k_ff_7 (
    .J(j_k_ff_3_q), .clk(clock_2_out), .K(j_k_ff_3_q), .Q(j_k_ff_7_q));  // open: Qn, preset, reset
  LED led_6 (.in(j_k_ff_7_q));
  J_K_Flip_Flop j_k_ff_8 (
    .J(j_k_ff_4_q), .clk(clock_3_out), .K(j_k_ff_4_q), .Q(j_k_ff_8_q), .reset(and_3_out));  // open: Qn, preset
  LED led_7 (.in(j_k_ff_8_q));
  LED led_8 (.in(j_k_ff_1_q[1]));
  J_K_Flip_Flop j_k_ff_9 (
    .J(and_2_out), .clk(clock_4_out), .K(and_2_out), .Q(j_k_ff_1_q[2]), .reset(and_4_out));  // open: Qn, preset
  J_K_Flip_Flop j_k_ff_10 (
    .J(in_3), .K(in_3), .clk(clock_1_out), .Q(j_k_ff_10_q[0]), .reset(in_4));  // open: Qn, preset
  J_K_Flip_Flop j_k_ff_11 (
    .J(j_k_ff_7_q), .clk(clock_2_out), .K(j_k_ff_7_q), .Q(j_k_ff_11_q));  // open: Qn, preset, reset
  LED led_9 (.in(j_k_ff_11_q));
  and and_1 (and_1_out, j_k_ff_4_q, j_k_ff_8_q);
  J_K_Flip_Flop j_k_ff_12 (
    .J(and_1_out), .clk(clock_3_out), .K(and_1_out), .Q(j_k_ff_12_q), .reset(and_3_out));  // open: Qn, preset
  LED led_10 (.in(j_k_ff_12_q));
  and and_2 (and_2_out, j_k_ff_1_q[0], j_k_ff_1_q[1]);
  LED led_11 (.in(j_k_ff_1_q[2]));
  LED led_12 (.in(j_k_ff_10_q[0]));
  and and_3 (and_3_out, j_k_ff_12_q, j_k_ff_8_q);
  and and_4 (and_4_out, j_k_ff_1_q[2], j_k_ff_1_q[1]);
  Hex_Digit_Display hex_digit_display_1 (.value({in_5, j_k_ff_10_q}));  // open: dp
  Hex_Digit_Display hex_digit_display_2 (.value({in_2, j_k_ff_1_q}));  // open: dp
endmodule
