// Logisim project lab_04.circ as structural Verilog: 1 circuit, main circuit main
module main (
  input  in_1,
  input  in_2,
  input  L_R_Control,
  input  Input,
  input  in_5,
  input  in_6
);

  wire and_1_out, and_2_out, clock_1_out, clock_2_out, d_ff_1_q, d_ff_2_q, d_ff_3_q, d_ff_4_q, d_ff_5_q,
       d_ff_6_q, d_ff_7_q, nand_1_out, nand_2_out, nand_3_out, nand_4_out, nand_5_out, nand_6_out,
       nand_7_out, nand_8_out, nand_9_out, nand_10_out, nand_11_out, nand_12_out, nand_13_out, nand_14_out,
       nand_15_out, nand_16_out, nand_17_out, nand_18_out, nand_19_out, nand_20_out, nand_21_out, not_1_out,
       not_2_out, not_3_out;

  Clock clock_1 (.out(clock_1_out));
  not not_1 (not_1_out, in_2);
  not not_2 (not_2_out, L_R_Control);
  Clock clock_2 (.out(clock_2_out));
  not not_3 (not_3_out, in_5);
  nand nand_1 (nand_1_out, d_ff_3_q, not_3_out);
  nand nand_2 (nand_2_out, in_5, in_6);
  D_Flip_Flop d_ff_1 (.D(nand_5_out), .clk(clock_1_out), .Q(d_ff_1_q));  // open: Qn, preset, reset
  and and_1 (and_1_out, not_1_out, in_1);
  and and_2 (and_2_out, in_1, in_2);
  nand nand_3 (nand_3_out, d_ff_4_q, not_2_out);
  nand nand_4 (nand_4_out, L_R_Control, Input);
  D_Flip_Flop d_ff_2 (.D(nand_6_out), .clk(clock_2_out), .Q(d_ff_2_q));  // open: Qn, preset, reset
  nand nand_5 (nand_5_out, nand_1_out, nand_2_out);
  LED led_1 (.in(d_ff_1_q));
  LED led_2 (.in(and_1_out));
  LED led_3 (.in(and_2_out));
  LED led_4 (.in(d_ff_2_q));
  nand nand_6 (nand_6_out, nand_3_out, nand_4_out);
  nand nand_7 (nand_7_out, not_3_out, in_6);
  nand nand_8 (nand_8_out, in_5, d_ff_1_q);
  D_Flip_Flop d_ff_3 (.D(nand_11_out), .clk(clock_1_out), .Q(d_ff_3_q));  // open: Qn, preset, reset
  nand nand_9 (nand_9_out, d_ff_5_q, not_2_out);
  nand nand_10 (nand_10_out, L_R_Control, d_ff_2_q);
  D_Flip_Flop d_ff_4 (.D(nand_12_out), .clk(clock_2_out), .Q(d_ff_4_q));  // open: Qn, preset, reset
  nand nand_11 (nand_11_out, nand_7_out, nand_8_out);
  LED led_5 (.in(d_ff_3_q));
  nand nand_12 (nand_12_out, nand_9_out, nand_10_out);
  LED led_6 (.in(d_ff_4_q));
  nand nand_13 (nand_13_out, d_ff_6_q, not_2_out);
  nand nand_14 (nand_14_out, L_R_Control, d_ff_4_q);
  D_Flip_Flop d_ff_5 (.D(nand_15_out), .clk(clock_2_out), .Q(d_ff_5_q));  // open: Qn, preset, reset
  nand nand_15 (nand_15_out, nand_13_out, nand_14_out);
  LED led_7 (.in(d_ff_5_q));
  nand nand_16 (nand_16_out, d_ff_7_q, not_2_out);
  nand nand_17 (nand_17_out, L_R_Control, d_ff_5_q);
  D_Flip_Flop d_ff_6 (.D(nand_18_out), .clk(clock_2_out), .Q(d_ff_6_q));  // open: Qn, preset, reset
  nand nand_18 (nand_18_out, nand_16_out, nand_17_out);
  LED led_8 (.in(d_ff_6_q));
  nand nand_19 (nand_19_out, Input, not_2_out);
  nand nand_20 (nand_20_out, L_R_Control, d_ff_6_q);
  D_Flip_Flop d_ff_7 (.D(nand_21_out), .clk(clock_2_out), .Q(d_ff_7_q));  // open: Qn, preset, reset
  nand nand_21 (nand_21_out, nand_19_out, nand_20_out);
  LED led_9 (.in(d_ff_7_q));

  // Notes on the sheet:
  //   Clock
endmodule
