// Logisim project Clock.circ as structural Verilog: 11 circuits, main circuit Clockwork
module Clockwork (
  input  Enable
);

  wire _2_Hz_ticker_out, bot_1_a0, bot_1_a1, bot_1_a2, bot_1_a3, bot_1_b0, bot_1_b1, bot_1_b2, bot_1_b3,
       bot_1_c0, bot_1_c1, bot_1_c2, bot_1_c3, bot_1_d0, bot_1_d1, bot_1_d2, bot_1_d3, bot_1_e0, bot_1_e1,
       bot_1_e2, bot_1_e3, bot_1_f0, bot_1_f1, bot_1_f2, bot_1_f3, plus_1_hour_out, plus_1_minute_out,
       plus_1_second_out, timer_1_enablen, timer_1_enables, top_1_a0, top_1_a1, top_1_a2, top_1_a3, top_1_b0,
       top_1_b1, top_1_b2, top_1_b3, top_1_c0, top_1_c1, top_1_c2, top_1_c3, top_1_d0, top_1_d1, top_1_d2,
       top_1_d3, top_1_e0, top_1_e1, top_1_e2, top_1_e3, top_1_f0, top_1_f1, top_1_f2, top_1_f3;
  wire [5:0] timer_1_hourn, timer_1_hours, timer_1_minn, timer_1_mins, timer_1_secn, timer_1_secs;

  Clock _2_Hz_ticker (.out(_2_Hz_ticker_out));
  Button plus_1_second (.out(plus_1_second_out));
  Button plus_1_minute (.out(plus_1_minute_out));
  Button plus_1_hour (.out(plus_1_hour_out));
  Timer timer_1 (
    .Clock(_2_Hz_ticker_out), .enable(Enable), .sec(plus_1_second_out), .min(plus_1_minute_out),
    .hour(plus_1_hour_out), .enableN(timer_1_enablen), .hourN(timer_1_hourn), .minN(timer_1_minn),
    .secN(timer_1_secn), .enableS(timer_1_enables), .hourS(timer_1_hours), .minS(timer_1_mins),
    .secS(timer_1_secs));
  Top top_1 (
    .enable(timer_1_enablen), .hour(timer_1_hourn), .min(timer_1_minn), .sec(timer_1_secn), .f3(top_1_f3),
    .f2(top_1_f2), .f1(top_1_f1), .f0(top_1_f0), .e3(top_1_e3), .e2(top_1_e2), .e1(top_1_e1), .e0(top_1_e0),
    .d3(top_1_d3), .d2(top_1_d2), .d1(top_1_d1), .d0(top_1_d0), .c3(top_1_c3), .c2(top_1_c2), .c1(top_1_c1),
    .c0(top_1_c0), .b3(top_1_b3), .b2(top_1_b2), .b1(top_1_b1), .b0(top_1_b0), .a3(top_1_a3), .a2(top_1_a2),
    .a1(top_1_a1), .a0(top_1_a0));  // open: NO2, NO1
  _7_Segment_Display u_7_segment_display_1 (
    .g(top_1_e3), .f(top_1_e2), .a(top_1_e1), .b(top_1_e0), .e(bot_1_e3), .d(bot_1_e2), .c(bot_1_e1),
    .dp(bot_1_e0));
  _7_Segment_Display u_7_segment_display_2 (
    .g(top_1_f3), .f(top_1_f2), .a(top_1_f1), .b(top_1_f0), .e(bot_1_f3), .d(bot_1_f2), .c(bot_1_f1),
    .dp(bot_1_f0));
  Bot bot_1 (
    .sec(timer_1_secs), .min(timer_1_mins), .hour(timer_1_hours), .enable(timer_1_enables), .f3(bot_1_f3),
    .f2(bot_1_f2), .f1(bot_1_f1), .f0(bot_1_f0), .e3(bot_1_e3), .e2(bot_1_e2), .e1(bot_1_e1), .e0(bot_1_e0),
    .d3(bot_1_d3), .d2(bot_1_d2), .d1(bot_1_d1), .d0(bot_1_d0), .c3(bot_1_c3), .c2(bot_1_c2), .c1(bot_1_c1),
    .c0(bot_1_c0), .b3(bot_1_b3), .b2(bot_1_b2), .b1(bot_1_b1), .b0(bot_1_b0), .a3(bot_1_a3), .a2(bot_1_a2),
    .a1(bot_1_a1), .a0(bot_1_a0));  // open: NO2, NO1
  _7_Segment_Display u_7_segment_display_3 (
    .g(top_1_c3), .f(top_1_c2), .a(top_1_c1), .b(top_1_c0), .e(bot_1_c3), .d(bot_1_c2), .c(bot_1_c1),
    .dp(bot_1_c0));
  _7_Segment_Display u_7_segment_display_4 (
    .g(top_1_d3), .f(top_1_d2), .a(top_1_d1), .b(top_1_d0), .e(bot_1_d3), .d(bot_1_d2), .c(bot_1_d1),
    .dp(bot_1_d0));
  _7_Segment_Display u_7_segment_display_5 (
    .g(top_1_a3), .f(top_1_a2), .a(top_1_a1), .b(top_1_a0), .e(bot_1_a3), .d(bot_1_a2), .c(bot_1_a1),
    .dp(bot_1_a0));
  _7_Segment_Display u_7_segment_display_6 (
    .g(top_1_b3), .f(top_1_b2), .a(top_1_b1), .b(top_1_b0), .e(bot_1_b3), .d(bot_1_b2), .c(bot_1_b1),
    .dp(bot_1_b0));

  // Notes on the sheet:
  //   How to use:
  //   This is the top level circuit
  //   Set the Enable pin below to 1
  //   This circuit is supposed to mimic a digital 24-hour clock
  //   Under the "Simulate" menu: Set Tick frequency to 2 Hz
  //   Click the 3 "+1" buttons until the watch has matched up with the real world
  //   Top and Bottom do similar things, 
  //   but for their own part of the 7-Segment displays
  //   This is only so this top-circuit can look more simple
endmodule

module Timer (
  input  Clock,
  input  enable,
  input  sec,
  input  min,
  input  hour,
  output enableN,
  output [5:0] hourN,
  output [5:0] minN,
  output [5:0] secN,
  output enableS,
  output [5:0] hourS,
  output [5:0] minS,
  output [5:0] secS
);

  wire Minutes_overflow, Seconds_overflow;

  _59 Seconds (
    .Clock(Clock), .in_2(sec), .Enable(enable), .s0(secN[0]), .s1(secN[1]), .s2(secN[2]), .s3(secN[3]),
    .s4(secN[4]), .s5(secN[5]), .overflow(Seconds_overflow));
  _59 Minutes (
    .Clock(Seconds_overflow), .in_2(min), .Enable(enable), .s0(minN[0]), .s1(minN[1]), .s2(minN[2]),
    .s3(minN[3]), .s4(minN[4]), .s5(minN[5]), .overflow(Minutes_overflow));
  _23 u_Hours (
    .Clock(Minutes_overflow), .in_2(hour), .Enable(enable), .s0(hourN[0]), .s1(hourN[1]), .s2(hourN[2]),
    .s3(hourN[3]), .s4(hourN[4]), .s5(hourN[5]));  // open: overflow

  assign enableN = enable;
  assign enableS = enable;
  assign hourS = hourN;
  assign minS = minN;
  assign secS = secN;

  // Notes on the sheet:
  //   And likewise "Hours" only counts up when "Minutes have counted to 59 and reset
  //   The role of this circuit is to take
  //   user input and the clock signal.
  //   Hours, Minutes and Seconds.
  //   which it uses to count seconds.
  //   in place of the clock-signal.
  //   have counted to 59 and reset
  //   Timer is placed once within "Clockwork"
  //   With those, it generates 3 signals:
  //   All this work happens exclusively
  //   inside the 3 subcircuits which are almost identical
  //   Enable, and the time signals are routed to 2 places
  //   Both Top and Bottom needs the whole thing to work
  //   Only the upper circuit receives the actual Clock
  //   Minutes are counted by receiving the Second-overflow
  //   So "Minutes" only counts up when "Seconds"
endmodule

module Top (
  input  enable,
  input  [5:0] hour,
  input  [5:0] min,
  input  [5:0] sec,
  output f3,
  output f2,
  output f1,
  output f0,
  output e3,
  output e2,
  output e1,
  output e0,
  output NO2,
  output d3,
  output d2,
  output d1,
  output d0,
  output c3,
  output c2,
  output c1,
  output c0,
  output NO1,
  output b3,
  output b2,
  output b1,
  output b0,
  output a3,
  output a2,
  output a1,
  output a0
);

  wire hexdecc1_1_v0, hexdecc1_1_v1, hexdecc1_1_v2, hexdecc1_1_v3, hexdecc1_2_v0, hexdecc1_2_v1,
       hexdecc1_2_v2, hexdecc1_2_v3, hexdecc1_3_v0, hexdecc1_3_v1, hexdecc1_3_v2, hexdecc1_3_v3,
       hexdecc2_1_v0, hexdecc2_1_v1, hexdecc2_1_v2, hexdecc2_1_v3, hexdecc2_2_v0, hexdecc2_2_v1,
       hexdecc2_2_v2, hexdecc2_2_v3, hexdecc2_3_v0, hexdecc2_3_v1, hexdecc2_3_v2, hexdecc2_3_v3;

  HexDecc2 hexdecc2_1 (
    .t5(hour[5]), .t4(hour[4]), .t3(hour[3]), .t2(hour[2]), .t1(hour[1]), .t0(hour[0]), .v3(hexdecc2_1_v3),
    .v2(hexdecc2_1_v2), .v1(hexdecc2_1_v1), .v0(hexdecc2_1_v0));
  DigitTop digittop_1 (
    .Enable(enable), .v3(hexdecc2_1_v3), .v2(hexdecc2_1_v2), .v1(hexdecc2_1_v1), .v0(hexdecc2_1_v0), .d3(f3),
    .d2(f2), .d1(f1), .d0(f0));
  HexDecc1 hexdecc1_1 (
    .t5(hour[5]), .t4(hour[4]), .t3(hour[3]), .t2(hour[2]), .t1(hour[1]), .t0(hour[0]), .v3(hexdecc1_1_v3),
    .v2(hexdecc1_1_v2), .v1(hexdecc1_1_v1), .v0(hexdecc1_1_v0));
  DigitTop digittop_2 (
    .Enable(enable), .v3(hexdecc1_1_v3), .v2(hexdecc1_1_v2), .v1(hexdecc1_1_v1), .v0(hexdecc1_1_v0), .d3(e3),
    .d2(e2), .d1(e1), .d0(e0));
  HexDecc2 hexdecc2_2 (
    .t5(min[5]), .t4(min[4]), .t3(min[3]), .t2(min[2]), .t1(min[1]), .t0(min[0]), .v3(hexdecc2_2_v3),
    .v2(hexdecc2_2_v2), .v1(hexdecc2_2_v1), .v0(hexdecc2_2_v0));
  DigitTop digittop_3 (
    .Enable(enable), .v3(hexdecc2_2_v3), .v2(hexdecc2_2_v2), .v1(hexdecc2_2_v1), .v0(hexdecc2_2_v0), .d3(d3),
    .d2(d2), .d1(d1), .d0(d0));
  HexDecc1 hexdecc1_2 (
    .t5(min[5]), .t4(min[4]), .t3(min[3]), .t2(min[2]), .t1(min[1]), .t0(min[0]), .v3(hexdecc1_2_v3),
    .v2(hexdecc1_2_v2), .v1(hexdecc1_2_v1), .v0(hexdecc1_2_v0));
  DigitTop digittop_4 (
    .Enable(enable), .v3(hexdecc1_2_v3), .v2(hexdecc1_2_v2), .v1(hexdecc1_2_v1), .v0(hexdecc1_2_v0), .d3(c3),
    .d2(c2), .d1(c1), .d0(c0));
  HexDecc2 hexdecc2_3 (
    .t5(sec[5]), .t4(sec[4]), .t3(sec[3]), .t2(sec[2]), .t1(sec[1]), .t0(sec[0]), .v3(hexdecc2_3_v3),
    .v2(hexdecc2_3_v2), .v1(hexdecc2_3_v1), .v0(hexdecc2_3_v0));
  DigitTop digittop_5 (
    .Enable(enable), .v3(hexdecc2_3_v3), .v2(hexdecc2_3_v2), .v1(hexdecc2_3_v1), .v0(hexdecc2_3_v0), .d3(b3),
    .d2(b2), .d1(b1), .d0(b0));
  HexDecc1 hexdecc1_3 (
    .t5(sec[5]), .t4(sec[4]), .t3(sec[3]), .t2(sec[2]), .t1(sec[1]), .t0(sec[0]), .v3(hexdecc1_3_v3),
    .v2(hexdecc1_3_v2), .v1(hexdecc1_3_v1), .v0(hexdecc1_3_v0));
  DigitTop digittop_6 (
    .Enable(enable), .v3(hexdecc1_3_v3), .v2(hexdecc1_3_v2), .v1(hexdecc1_3_v1), .v0(hexdecc1_3_v0), .d3(a3),
    .d2(a2), .d1(a1), .d0(a0));

  assign NO1 = 1'b0;
  assign NO2 = 1'b0;

  // Notes on the sheet:
  //   This circuit exists once within "Clockwork"
  //   Top is designed to match up with
  //   6 7-segment displays placed below it
  //   No work is done here, rather signals
  //   are being moved to other subcircuits
  //   while the 3 middle "HexDecc1" handle the "ones"
  //   that handle the different responsibilities in separate smaller tasks. 
  //   The 3 top circuits "HexDecc2" handle the "tens" from any 6-bit number, 
  //   but only for the TOP part of the 7-Seg display!   Look in "Clockwork" to see why.
  //   The 6 lowest "DigitTop" circuits converts a binary number into the correct 7-Segment signals
endmodule

module Bot (
  input  [5:0] sec,
  input  [5:0] min,
  input  [5:0] hour,
  input  enable,
  output f3,
  output f2,
  output f1,
  output f0,
  output e3,
  output e2,
  output e1,
  output e0,
  output NO2,
  output d3,
  output d2,
  output d1,
  output d0,
  output c3,
  output c2,
  output c1,
  output c0,
  output NO1,
  output b3,
  output b2,
  output b1,
  output b0,
  output a3,
  output a2,
  output a1,
  output a0
);

  wire hexdecc1_1_v0, hexdecc1_1_v1, hexdecc1_1_v2, hexdecc1_1_v3, hexdecc1_2_v0, hexdecc1_2_v1,
       hexdecc1_2_v2, hexdecc1_2_v3, hexdecc1_3_v0, hexdecc1_3_v1, hexdecc1_3_v2, hexdecc1_3_v3,
       hexdecc2_1_v0, hexdecc2_1_v1, hexdecc2_1_v2, hexdecc2_1_v3, hexdecc2_2_v0, hexdecc2_2_v1,
       hexdecc2_2_v2, hexdecc2_2_v3, hexdecc2_3_v0, hexdecc2_3_v1, hexdecc2_3_v2, hexdecc2_3_v3;

  DigitBot digitbot_1 (
    .Enable(enable), .d3(f3), .d2(f2), .d1(f1), .d0(f0), .v3(hexdecc2_1_v3), .v2(hexdecc2_1_v2),
    .v1(hexdecc2_1_v1), .v0(hexdecc2_1_v0));
  HexDecc2 hexdecc2_1 (
    .t5(hour[5]), .t4(hour[4]), .t3(hour[3]), .t2(hour[2]), .t1(hour[1]), .t0(hour[0]), .v3(hexdecc2_1_v3),
    .v2(hexdecc2_1_v2), .v1(hexdecc2_1_v1), .v0(hexdecc2_1_v0));
  DigitBot digitbot_2 (
    .Enable(enable), .d3(e3), .d2(e2), .d1(e1), .d0(e0), .v3(hexdecc1_1_v3), .v2(hexdecc1_1_v2),
    .v1(hexdecc1_1_v1), .v0(hexdecc1_1_v0));
  HexDecc1 hexdecc1_1 (
    .t5(hour[5]), .t4(hour[4]), .t3(hour[3]), .t2(hour[2]), .t1(hour[1]), .t0(hour[0]), .v3(hexdecc1_1_v3),
    .v2(hexdecc1_1_v2), .v1(hexdecc1_1_v1), .v0(hexdecc1_1_v0));
  DigitBot digitbot_3 (
    .Enable(enable), .d3(d3), .d2(d2), .d1(d1), .d0(d0), .v3(hexdecc2_2_v3), .v2(hexdecc2_2_v2),
    .v1(hexdecc2_2_v1), .v0(hexdecc2_2_v0));
  HexDecc2 hexdecc2_2 (
    .t5(min[5]), .t4(min[4]), .t3(min[3]), .t2(min[2]), .t1(min[1]), .t0(min[0]), .v3(hexdecc2_2_v3),
    .v2(hexdecc2_2_v2), .v1(hexdecc2_2_v1), .v0(hexdecc2_2_v0));
  DigitBot digitbot_4 (
    .Enable(enable), .d3(c3), .d2(c2), .d1(c1), .d0(c0), .v3(hexdecc1_2_v3), .v2(hexdecc1_2_v2),
    .v1(hexdecc1_2_v1), .v0(hexdecc1_2_v0));
  HexDecc1 hexdecc1_2 (
    .t5(min[5]), .t4(min[4]), .t3(min[3]), .t2(min[2]), .t1(min[1]), .t0(min[0]), .v3(hexdecc1_2_v3),
    .v2(hexdecc1_2_v2), .v1(hexdecc1_2_v1), .v0(hexdecc1_2_v0));
  DigitBot digitbot_5 (
    .Enable(enable), .d3(b3), .d2(b2), .d1(b1), .d0(b0), .v3(hexdecc2_3_v3), .v2(hexdecc2_3_v2),
    .v1(hexdecc2_3_v1), .v0(hexdecc2_3_v0));
  HexDecc2 hexdecc2_3 (
    .t5(sec[5]), .t4(sec[4]), .t3(sec[3]), .t2(sec[2]), .t1(sec[1]), .t0(sec[0]), .v3(hexdecc2_3_v3),
    .v2(hexdecc2_3_v2), .v1(hexdecc2_3_v1), .v0(hexdecc2_3_v0));
  DigitBot digitbot_6 (
    .Enable(enable), .d3(a3), .d2(a2), .d1(a1), .d0(a0), .v3(hexdecc1_3_v3), .v2(hexdecc1_3_v2),
    .v1(hexdecc1_3_v1), .v0(hexdecc1_3_v0));
  HexDecc1 hexdecc1_3 (
    .t5(sec[5]), .t4(sec[4]), .t3(sec[3]), .t2(sec[2]), .t1(sec[1]), .t0(sec[0]), .v3(hexdecc1_3_v3),
    .v2(hexdecc1_3_v2), .v1(hexdecc1_3_v1), .v0(hexdecc1_3_v0));

  assign NO1 = 1'b0;
  assign NO2 = 1'b0;

  // Notes on the sheet:
  //   in comparison to Top
  //   This circuit exists once within "Clockwork"
  //   This contains almost the same sub components as the "Top" circuit, and does all the same work
  //   Instead of "DigitTop" it has "DigitBot" circuits, and the whole thing is basically placed upside down
endmodule

module DigitTop (
  input  v3,
  input  v2,
  input  v1,
  input  v0,
  input  Enable,
  output d3,
  output d2,
  output d1,
  output d0
);

  wire and_1_out, and_2_out, and_3_out, and_4_out, and_5_out, and_6_out, and_7_out, and_8_out, and_9_out,
       and_10_out, and_11_out, and_12_out, and_13_out, and_14_out, and_15_out, and_16_out, and_17_out,
       and_18_out, and_19_out, and_20_out, and_21_out, and_22_out, not_1_out, not_2_out, not_3_out,
       not_4_out, not_5_out, not_6_out, not_7_out, not_8_out, not_9_out, not_10_out, not_11_out, not_12_out,
       not_13_out, not_14_out, not_15_out, not_16_out, not_17_out, not_18_out, not_19_out, not_20_out,
       not_21_out, not_22_out, not_23_out, not_24_out, not_25_out, not_26_out, not_27_out, not_28_out,
       not_29_out, or_1_out, or_2_out, or_3_out, or_4_out;

  not not_1 (not_1_out, v2);
  not not_2 (not_2_out, v0);
  not not_3 (not_3_out, v3);
  not not_4 (not_4_out, v1);
  not not_5 (not_5_out, v2);
  not not_6 (not_6_out, v1);
  not not_7 (not_7_out, v0);
  not not_8 (not_8_out, v3);
  not not_9 (not_9_out, v1);
  not not_10 (not_10_out, v0);
  not not_11 (not_11_out, v2);
  not not_12 (not_12_out, v2);
  not not_13 (not_13_out, v0);
  not not_14 (not_14_out, v3);
  not not_15 (not_15_out, v3);
  not not_16 (not_16_out, v2);
  not not_17 (not_17_out, v1);
  not not_18 (not_18_out, v0);
  not not_19 (not_19_out, v3);
  not not_20 (not_20_out, v2);
  not not_21 (not_21_out, v3);
  not not_22 (not_22_out, v1);
  not not_23 (not_23_out, v0);
  not not_24 (not_24_out, v2);
  not not_25 (not_25_out, v1);
  not not_26 (not_26_out, v2);
  not not_27 (not_27_out, v0);
  not not_28 (not_28_out, v3);
  not not_29 (not_29_out, v1);
  and and_1 (and_1_out, not_1_out, v1);
  and and_2 (and_2_out, v1, not_2_out);
  and and_3 (and_3_out, not_3_out, v2, not_4_out);
  and and_4 (and_4_out, v3, not_5_out);
  and and_5 (and_5_out, v3, v0);
  and and_6 (and_6_out, not_6_out, not_7_out);
  and and_7 (and_7_out, not_8_out, v2, not_9_out);
  and and_8 (and_8_out, v2, not_10_out);
  and and_9 (and_9_out, v3, not_11_out);
  and and_10 (and_10_out, v3, v1);
  and and_11 (and_11_out, not_12_out, not_13_out);
  and and_12 (and_12_out, not_14_out, v1);
  and and_13 (and_13_out, not_15_out, v2, v0);
  and and_14 (and_14_out, v2, v1);
  and and_15 (and_15_out, v3, not_16_out, not_17_out);
  and and_16 (and_16_out, v3, not_18_out);
  and and_17 (and_17_out, not_19_out, not_20_out);
  and and_18 (and_18_out, not_21_out, not_22_out, not_23_out);
  and and_19 (and_19_out, not_24_out, not_25_out);
  and and_20 (and_20_out, not_26_out, not_27_out);
  and and_21 (and_21_out, not_28_out, v1, v0);
  and and_22 (and_22_out, v3, not_29_out, v0);
  or or_1 (or_1_out, and_1_out, and_2_out, and_3_out, and_4_out, and_5_out);
  or or_2 (or_2_out, and_6_out, and_7_out, and_8_out, and_9_out, and_10_out);
  or or_3 (or_3_out, and_11_out, and_12_out, and_13_out, and_14_out, and_15_out, and_16_out);
  or or_4 (or_4_out, and_17_out, and_18_out, and_19_out, and_20_out, and_21_out, and_22_out);
  and and_23 (d3, Enable, or_1_out);
  and and_24 (d2, Enable, or_2_out);
  and and_25 (d0, Enable, or_4_out);
  and and_26 (d1, Enable, or_3_out);

  // Notes on the sheet:
  //   It is called DigitTop
  //   This circuit exists 6 times, within "Top"
  //   and then Logisim automatically built this circuit
  //   It receives a 4-bit number and delivers a 4-bit number
  //   that correctly draws the digit on the top part of a 7-Segment display
  //   This circuits logic was created by using Logisims built in tools
  //   and so, inputs and outputs was put into a Truth table
  //   When enable is 0, all outputs are 0
  //   else, outputs are unchanged
  //   After auto-building, the "Enable" signal was added
endmodule

module tests (
  input  in_1,
  input  in_2,
  input  in_3,
  input  in_4,
  input  in_5,
  input  [3:0] in_6,
  input  in_7,
  input  [3:0] in_8
);

  wire and_1_out, and_2_out, button_1_out, clock_1_out, DigitBot_d0, DigitBot_d1, DigitBot_d2, DigitBot_d3,
       DigitTop_d0, DigitTop_d1, DigitTop_d2, DigitTop_d3, not_1_out, not_2_out, not_3_out, not_4_out,
       not_5_out, not_6_out, not_7_out, or_1_out, or_2_out, or_3_out, or_4_out, or_5_out, t_ff_1_q,
       t_ff_1_qn, t_ff_2_q, t_ff_2_qn, t_ff_3_q, t_ff_3_qn, t_ff_4_q;

  _7_Segment_Display u_7_segment_display_1 (
    .g(in_6[3]), .f(in_6[2]), .a(in_6[1]), .b(in_6[0]), .e(in_8[3]), .d(in_8[2]), .c(in_8[1]), .dp(in_8[0]));
  DigitTop DigitTop (
    .Enable(in_7), .v3(in_1), .v2(in_2), .v1(in_3), .v0(in_4), .d3(DigitTop_d3), .d2(DigitTop_d2),
    .d1(DigitTop_d1), .d0(DigitTop_d0));
  _7_Segment_Display u_7_segment_display_2 (
    .g(DigitTop_d3), .f(DigitTop_d2), .a(DigitTop_d1), .b(DigitTop_d0), .e(DigitBot_d3), .d(DigitBot_d2),
    .c(DigitBot_d1), .dp(DigitBot_d0));
  DigitBot DigitBot (
    .Enable(in_7), .d3(DigitBot_d3), .d2(DigitBot_d2), .d1(DigitBot_d1), .d0(DigitBot_d0), .v3(in_1),
    .v2(in_2), .v1(in_3), .v0(in_4));
  Button button_1 (.out(button_1_out));
  Clock clock_1 (.out(clock_1_out));
  not not_1 (not_1_out, clock_1_out);
  and and_1 (and_1_out, not_1_out, clock_1_out);
  not not_2 (not_2_out, in_5);
  not not_3 (not_3_out, in_5);
  not not_4 (not_4_out, in_5);
  not not_5 (not_5_out, in_5);
  T_Flip_Flop t_ff_1 (.clk(or_1_out), .T(in_5), .Q(t_ff_1_q), .Qn(t_ff_1_qn), .reset(or_2_out));  // open: preset, en
  or or_1 (or_1_out, button_1_out, and_1_out);
  or or_2 (or_2_out, not_2_out, and_2_out);
  T_Flip_Flop t_ff_2 (.clk(t_ff_1_qn), .T(in_5), .Q(t_ff_2_q), .Qn(t_ff_2_qn), .reset(or_3_out));  // open: preset, en
  or or_3 (or_3_out, not_3_out, and_2_out);
  T_Flip_Flop t_ff_3 (.clk(t_ff_2_qn), .T(in_5), .Q(t_ff_3_q), .Qn(t_ff_3_qn), .reset(or_4_out));  // open: preset, en
  or or_4 (or_4_out, not_4_out, and_2_out);
  T_Flip_Flop t_ff_4 (.clk(t_ff_3_qn), .T(in_5), .Q(t_ff_4_q), .reset(or_5_out));  // open: Qn, preset, en
  or or_5 (or_5_out, not_5_out, and_2_out);
  not not_6 (not_6_out, t_ff_1_q);
  not not_7 (not_7_out, t_ff_2_q);
  and and_2 (and_2_out, not_6_out, not_7_out, t_ff_3_q, t_ff_4_q);

  // Notes on the sheet:
  //   This circuit is only used for testing, and does not have anything to do with the rest.
endmodule

module DigitBot (
  input  Enable,
  input  v3,
  input  v2,
  input  v1,
  input  v0,
  output d3,
  output d2,
  output d1,
  output d0
);

  wire and_1_out, and_2_out, and_3_out, and_4_out, and_5_out, and_6_out, and_7_out, and_8_out, and_9_out,
       and_10_out, and_11_out, and_12_out, and_13_out, and_14_out, not_1_out, not_2_out, not_3_out,
       not_4_out, not_5_out, not_6_out, not_7_out, not_8_out, not_9_out, not_10_out, not_11_out, not_12_out,
       not_13_out, not_14_out, not_15_out, not_16_out, or_1_out, or_2_out, or_3_out;

  not not_1 (not_1_out, v2);
  not not_2 (not_2_out, v0);
  not not_3 (not_3_out, v0);
  not not_4 (not_4_out, v3);
  not not_5 (not_5_out, v2);
  not not_6 (not_6_out, v0);
  not not_7 (not_7_out, v2);
  not not_8 (not_8_out, v1);
  not not_9 (not_9_out, v0);
  not not_10 (not_10_out, v1);
  not not_11 (not_11_out, v3);
  not not_12 (not_12_out, v1);
  not not_13 (not_13_out, v3);
  not not_14 (not_14_out, v1);
  not not_15 (not_15_out, v3);
  not not_16 (not_16_out, v2);
  and and_1 (and_1_out, not_1_out, not_2_out);
  and and_2 (and_2_out, v1, not_3_out);
  and and_3 (and_3_out, v3, v1);
  and and_4 (and_4_out, v3, v2);
  and and_5 (and_5_out, not_4_out, not_5_out, not_6_out);
  and and_6 (and_6_out, not_7_out, v1, v0);
  and and_7 (and_7_out, v2, not_8_out, v0);
  and and_8 (and_8_out, v2, v1, not_9_out);
  and and_9 (and_9_out, v3, not_10_out);
  and and_10 (and_10_out, not_11_out, not_12_out);
  and and_11 (and_11_out, not_13_out, v0);
  and and_12 (and_12_out, not_14_out, v0);
  and and_13 (and_13_out, not_15_out, v2);
  and and_14 (and_14_out, v3, not_16_out);
  and and_15 (d3, or_1_out, Enable);
  or or_1 (or_1_out, and_1_out, and_2_out, and_3_out, and_4_out);
  or or_2 (or_2_out, and_5_out, and_6_out, and_7_out, and_8_out, and_9_out);
  or or_3 (or_3_out, and_10_out, and_11_out, and_12_out, and_13_out, and_14_out);
  and and_16 (d2, or_2_out, Enable);
  and and_17 (d1, or_3_out, Enable);

  assign d0 = 1'b0;

  // Notes on the sheet:
  //   It is called DigitBot
  //   When enable is 0, all outputs are 0
  //   else, outputs are unchanged
  //   This circuit exists 6 times, within "Bottom"
  //   It receives a 4-bit number and delivers a 4-bit number
  //   and so, inputs and outputs was put into a Truth table
  //   and then Logisim automatically built this circuit
  //   After auto-building, the "Enable" signal was added
  //   that correctly draws the digit on the bottom part of a 7-Segment display
  //   This circuits logic was created by using Logisims built in tools
endmodule

module _59 (
  input  Clock,
  input  in_2,
  input  Enable,
  output s0,
  output s1,
  output s2,
  output s3,
  output s4,
  output s5,
  output overflow
);

  wire and_1_out, not_1_out, not_2_out, not_3_out, not_4_out, not_5_out, not_6_out, not_7_out, not_8_out,
       not_9_out, or_1_out, or_2_out, or_3_out, or_4_out, or_5_out, or_6_out, or_7_out, t_ff_1_qn, t_ff_2_qn,
       t_ff_3_qn, t_ff_4_qn, t_ff_5_qn;

  not not_1 (not_1_out, Clock);
  and and_1 (and_1_out, not_1_out, Clock);
  not not_2 (not_2_out, Enable);
  not not_3 (not_3_out, Enable);
  not not_4 (not_4_out, Enable);
  not not_5 (not_5_out, Enable);
  not not_6 (not_6_out, Enable);
  not not_7 (not_7_out, Enable);
  and and_2 (overflow, not_8_out, not_9_out, s2, s3, s4, s5);
  T_Flip_Flop t_ff_1 (.clk(or_1_out), .T(Enable), .Q(s0), .Qn(t_ff_1_qn), .reset(or_2_out));  // open: preset, en
  or or_1 (or_1_out, in_2, and_1_out);
  or or_2 (or_2_out, not_2_out, overflow);
  T_Flip_Flop t_ff_2 (.clk(t_ff_1_qn), .T(Enable), .Q(s1), .Qn(t_ff_2_qn), .reset(or_3_out));  // open: preset, en
  or or_3 (or_3_out, not_3_out, overflow);
  T_Flip_Flop t_ff_3 (.clk(t_ff_2_qn), .T(Enable), .Q(s2), .Qn(t_ff_3_qn), .reset(or_4_out));  // open: preset, en
  or or_4 (or_4_out, not_4_out, overflow);
  T_Flip_Flop t_ff_4 (.clk(t_ff_3_qn), .T(Enable), .Q(s3), .Qn(t_ff_4_qn), .reset(or_5_out));  // open: preset, en
  or or_5 (or_5_out, not_5_out, overflow);
  T_Flip_Flop t_ff_5 (.clk(t_ff_4_qn), .T(Enable), .Q(s4), .Qn(t_ff_5_qn), .reset(or_6_out));  // open: preset, en
  or or_6 (or_6_out, not_6_out, overflow);
  T_Flip_Flop t_ff_6 (.clk(t_ff_5_qn), .T(Enable), .Q(s5), .reset(or_7_out));  // open: Qn, preset, en
  or or_7 (or_7_out, not_7_out, overflow);
  not not_8 (not_8_out, s0);
  not not_9 (not_9_out, s1);

  // Notes on the sheet:
  //   This circuit exists 2 times within "Timer"
  //   This "59" circuit merely counts to 59
  //   and delivers an overflow signal and resets
  //   + is used like an instant asyncronous clock
  //   so the user can quickly add to the count
  //   When Enable is 0, the circuit is also reset
  //   This big AND gate detects 60 on the pins
  //   and then it instantly resets the system to 0
  //   and send it to the next flip-flop.
  //   Counting to 59 is used both
  //   for counting seconds and minutes
  //   Toggle flip-flops are used because
  //   they can halve the "clock-speed" 
  //   This perfectly mimics binary counting
endmodule

module _23 (
  input  Clock,
  input  in_2,
  input  Enable,
  output s0,
  output s1,
  output s2,
  output s3,
  output s4,
  output s5,
  output overflow
);

  wire and_1_out, not_1_out, not_2_out, not_3_out, not_4_out, not_5_out, not_6_out, not_7_out, not_8_out,
       not_9_out, not_10_out, not_11_out, or_1_out, or_2_out, or_3_out, or_4_out, or_5_out, or_6_out,
       or_7_out, t_ff_1_qn, t_ff_2_qn, t_ff_3_qn, t_ff_4_qn, t_ff_5_qn;

  not not_1 (not_1_out, Clock);
  and and_1 (and_1_out, not_1_out, Clock);
  not not_2 (not_2_out, Enable);
  not not_3 (not_3_out, Enable);
  not not_4 (not_4_out, Enable);
  not not_5 (not_5_out, Enable);
  not not_6 (not_6_out, Enable);
  not not_7 (not_7_out, Enable);
  and and_2 (overflow, not_8_out, not_9_out, not_10_out, s3, s4, not_11_out);
  T_Flip_Flop t_ff_1 (.clk(or_1_out), .T(Enable), .Q(s0), .Qn(t_ff_1_qn), .reset(or_2_out));  // open: preset, en
  or or_1 (or_1_out, in_2, and_1_out);
  or or_2 (or_2_out, not_2_out, overflow);
  T_Flip_Flop t_ff_2 (.clk(t_ff_1_qn), .T(Enable), .Q(s1), .Qn(t_ff_2_qn), .reset(or_3_out));  // open: preset, en
  or or_3 (or_3_out, not_3_out, overflow);
  T_Flip_Flop t_ff_3 (.clk(t_ff_2_qn), .T(Enable), .Q(s2), .Qn(t_ff_3_qn), .reset(or_4_out));  // open: preset, en
  or or_4 (or_4_out, not_4_out, overflow);
  T_Flip_Flop t_ff_4 (.clk(t_ff_3_qn), .T(Enable), .Q(s3), .Qn(t_ff_4_qn), .reset(or_5_out));  // open: preset, en
  or or_5 (or_5_out, not_5_out, overflow);
  T_Flip_Flop t_ff_5 (.clk(t_ff_4_qn), .T(Enable), .Q(s4), .Qn(t_ff_5_qn), .reset(or_6_out));  // open: preset, en
  or or_6 (or_6_out, not_6_out, overflow);
  T_Flip_Flop t_ff_6 (.clk(t_ff_5_qn), .T(Enable), .Q(s5), .reset(or_7_out));  // open: Qn, preset, en
  or or_7 (or_7_out, not_7_out, overflow);
  not not_8 (not_8_out, s0);
  not not_9 (not_9_out, s1);
  not not_10 (not_10_out, s2);
  not not_11 (not_11_out, s5);

  // Notes on the sheet:
  //   The "59" circuit was made first,
  //   and this one is just a copy with a
  //   different AND setup below
  //   This circuit exists once within "Timer"
  //   This "23" circuit merely counts to 23
  //   and delivers an overflow signal and resets
  //   + is used like an instant asyncronous clock
  //   so the user can quickly add to the count
  //   When Enable is 0, the circuit is also reset
  //   This big AND gate detects 24 on the pins
  //   and then it instantly resets the system to 0
  //   Toggle flip-flops are used because
  //   they can halve the "clock-speed" 
  //   and send it to the next flip-flop.
  //   Counting to 23 represents the hours
  //   This perfectly mimics binary counting
endmodule

module HexDecc1 (
  input  t5,
  input  t4,
  input  t3,
  input  t2,
  input  t1,
  input  t0,
  output v3,
  output v2,
  output v1,
  output v0
);

  wire and_1_out, and_2_out, and_3_out, and_4_out, and_5_out, and_6_out, and_7_out, and_8_out, and_9_out,
       and_10_out, and_11_out, and_12_out, and_13_out, and_14_out, and_15_out, and_16_out, and_17_out,
       and_18_out, and_19_out, and_20_out, and_21_out, and_22_out, and_23_out, not_1_out, not_2_out,
       not_3_out, not_4_out, not_5_out, not_6_out, not_7_out, not_8_out, not_9_out, not_10_out, not_11_out,
       not_12_out, not_13_out, not_14_out, not_15_out, not_16_out, not_17_out, not_18_out, not_19_out,
       not_20_out, not_21_out, not_22_out, not_23_out, not_24_out, not_25_out, not_26_out, not_27_out,
       not_28_out, not_29_out, not_30_out, not_31_out, not_32_out, not_33_out, not_34_out, not_35_out,
       not_36_out, not_37_out, not_38_out, not_39_out, not_40_out, not_41_out, not_42_out, not_43_out,
       not_44_out, not_45_out, not_46_out, not_47_out, not_48_out, not_49_out;

  not not_1 (not_1_out, t5);
  not not_2 (not_2_out, t4);
  not not_3 (not_3_out, t2);
  not not_4 (not_4_out, t1);
  not not_5 (not_5_out, t5);
  not not_6 (not_6_out, t3);
  not not_7 (not_7_out, t2);
  not not_8 (not_8_out, t1);
  not not_9 (not_9_out, t4);
  not not_10 (not_10_out, t3);
  not not_11 (not_11_out, t3);
  not not_12 (not_12_out, t2);
  not not_13 (not_13_out, t1);
  not not_14 (not_14_out, t4);
  not not_15 (not_15_out, t3);
  not not_16 (not_16_out, t1);
  not not_17 (not_17_out, t5);
  not not_18 (not_18_out, t4);
  not not_19 (not_19_out, t5);
  not not_20 (not_20_out, t2);
  not not_21 (not_21_out, t1);
  not not_22 (not_22_out, t5);
  not not_23 (not_23_out, t2);
  not not_24 (not_24_out, t2);
  not not_25 (not_25_out, t1);
  not not_26 (not_26_out, t4);
  not not_27 (not_27_out, t3);
  not not_28 (not_28_out, t2);
  not not_29 (not_29_out, t5);
  not not_30 (not_30_out, t4);
  not not_31 (not_31_out, t3);
  not not_32 (not_32_out, t5);
  not not_33 (not_33_out, t3);
  not not_34 (not_34_out, t5);
  not not_35 (not_35_out, t4);
  not not_36 (not_36_out, t1);
  not not_37 (not_37_out, t5);
  not not_38 (not_38_out, t3);
  not not_39 (not_39_out, t2);
  not not_40 (not_40_out, t1);
  not not_41 (not_41_out, t5);
  not not_42 (not_42_out, t2);
  not not_43 (not_43_out, t4);
  not not_44 (not_44_out, t3);
  not not_45 (not_45_out, t1);
  not not_46 (not_46_out, t3);
  not not_47 (not_47_out, t1);
  not not_48 (not_48_out, t4);
  not not_49 (not_49_out, t1);
  and and_1 (and_1_out, not_1_out, not_2_out, t3, not_3_out, not_4_out);
  and and_2 (and_2_out, not_5_out, t4, not_6_out, not_7_out, t1);
  and and_3 (and_3_out, t4, t3, t2, not_8_out);
  and and_4 (and_4_out, t5, not_9_out, not_10_out, t2, t1);
  and and_5 (and_5_out, t5, t4, not_11_out, not_12_out, not_13_out);
  and and_6 (and_6_out, t5, t4, t3, t1);
  and and_7 (and_7_out, not_14_out, not_15_out, t2, not_16_out);
  and and_8 (and_8_out, not_17_out, not_18_out, t2, t1);
  and and_9 (and_9_out, not_19_out, t4, not_20_out, not_21_out);
  and and_10 (and_10_out, not_22_out, t4, t3, not_23_out);
  and and_11 (and_11_out, t4, t3, not_24_out, not_25_out);
  and and_12 (and_12_out, t5, not_26_out, not_27_out, not_28_out, t1);
  and and_13 (and_13_out, t5, t3, t2);
  and and_14 (and_14_out, t5, t4, t2, t1);
  and and_15 (and_15_out, not_29_out, not_30_out, not_31_out, t1);
  and and_16 (and_16_out, not_32_out, not_33_out, t2, t1);
  and and_17 (and_17_out, not_34_out, not_35_out, t3, t2, not_36_out);
  and and_18 (and_18_out, not_37_out, t4, not_38_out, not_39_out, not_40_out);
  and and_19 (and_19_out, not_41_out, t4, t3, not_42_out, t1);
  and and_20 (and_20_out, t5, not_43_out, not_44_out, not_45_out);
  and and_21 (and_21_out, t5, not_46_out, t2, not_47_out);
  and and_22 (and_22_out, t5, not_48_out, t3, t1);
  and and_23 (and_23_out, t5, t4, t3, not_49_out);
  or or_1 (v3, and_1_out, and_2_out, and_3_out, and_4_out, and_5_out, and_6_out);
  or or_2 (v2, and_7_out, and_8_out, and_9_out, and_10_out, and_11_out, and_12_out, and_13_out, and_14_out);
  or or_3 (v1, and_15_out, and_16_out, and_17_out, and_18_out, and_19_out, and_20_out, and_21_out, and_22_out, and_23_out);

  assign v0 = t0;

  // Notes on the sheet:
  //   It is called HexDecc1
  //   or 0001 in 4-bit binary
  //   It receives a 6-bit number and delivers a 4-bit number
  //   that represents the "ones" of a decimal number
  //   Example: The number 110011 means 51,
  //   and so, the output value should be the "ones" value 1
  //   This circuits logic was created by using Logisims built in tools
  //   and so, inputs and outputs was put into a Truth table
  //   and then Logisim automatically built this circuit
  //   This circuit exists 3 times, both within "Top" and "Bottom"
endmodule

module HexDecc2 (
  input  t5,
  input  t4,
  input  t3,
  input  t2,
  input  t1,
  input  t0,
  output v3,
  output v2,
  output v1,
  output v0
);

  wire and_1_out, and_2_out, and_3_out, and_4_out, and_5_out, and_6_out, and_7_out, and_8_out, and_9_out,
       and_10_out, and_11_out, and_12_out, and_13_out, not_1_out, not_2_out, not_3_out, not_4_out, not_5_out,
       not_6_out, not_7_out, not_8_out, not_9_out, not_10_out, not_11_out, not_12_out, not_13_out,
       not_14_out, not_15_out, not_16_out;

  and and_1 (and_1_out, t5, t3);
  and and_2 (and_2_out, t5, t4);
  not not_1 (not_1_out, t5);
  not not_2 (not_2_out, t5);
  not not_3 (not_3_out, t4);
  not not_4 (not_4_out, t3);
  not not_5 (not_5_out, t5);
  not not_6 (not_6_out, t4);
  not not_7 (not_7_out, t5);
  not not_8 (not_8_out, t4);
  not not_9 (not_9_out, t5);
  not not_10 (not_10_out, t5);
  not not_11 (not_11_out, t3);
  not not_12 (not_12_out, t2);
  not not_13 (not_13_out, t4);
  not not_14 (not_14_out, t3);
  not not_15 (not_15_out, t3);
  not not_16 (not_16_out, t3);
  or or_1 (v2, and_1_out, and_2_out);
  and and_3 (and_3_out, not_1_out, t4, t2);
  and and_4 (and_4_out, not_2_out, t4, t3);
  and and_5 (and_5_out, t5, not_3_out, not_4_out);
  and and_6 (and_6_out, not_5_out, not_6_out, t3, t1);
  and and_7 (and_7_out, not_7_out, not_8_out, t3, t2);
  and and_8 (and_8_out, not_9_out, t3, t2, t1);
  and and_9 (and_9_out, not_10_out, t4, not_11_out, not_12_out);
  and and_10 (and_10_out, t5, not_13_out, not_14_out);
  and and_11 (and_11_out, t5, not_15_out, t1);
  and and_12 (and_12_out, t5, not_16_out, t2);
  and and_13 (and_13_out, t5, t4, t3);
  or or_2 (v1, and_3_out, and_4_out, and_5_out);
  or or_3 (v0, and_6_out, and_7_out, and_8_out, and_9_out, and_10_out, and_11_out, and_12_out, and_13_out);

  assign v3 = 1'b0;

  // Notes on the sheet:
  //   It is called HexDecc2
  //   or 0101 in 4-bit binary
  //   It receives a 6-bit number and delivers a 4-bit number
  //   that represents the "tens" of a decimal number
  //   Example: The number 110011 means 51,
  //   and so, the output value should be the "tens" value 5
  //   This circuits logic was created by using Logisims built in tools
  //   and so, inputs and outputs was put into a Truth table
  //   and then Logisim automatically built this circuit
  //   This circuit exists 3 times, both within "Top" and "Bottom"
endmodule
